// Logisim project Processor.circ as structural Verilog: 16 circuits, main circuit Processor
module Reg_8bit (
  input  Clock,
  input  Load,
  input  RST,
  input  En,
  input  I7,
  input  I6,
  input  I5,
  input  I4,
  input  I3,
  input  I2,
  input  I1,
  input  I0,
  output B7,
  output B6,
  output B5,
  output B4,
  output B3,
  output B2,
  output B1,
  output B0,
  output O7,
  output O6,
  output O5,
  output O4,
  output O3,
  output O2,
  output O1,
  output O0
);

  Register #(.width(1)) register_1 (.D(I7), .en(Load), .clk(Clock), .Q(B7), .clr(RST));
  Register #(.width(1)) register_2 (.D(I6), .en(Load), .clk(Clock), .Q(B6), .clr(RST));
  Register #(.width(1)) register_3 (.D(I5), .en(Load), .clk(Clock), .Q(B5), .clr(RST));
  Register #(.width(1)) register_4 (.D(I4), .en(Load), .clk(Clock), .Q(B4), .clr(RST));
  Register #(.width(1)) register_5 (.D(I3), .en(Load), .clk(Clock), .Q(B3), .clr(RST));
  Register #(.width(1)) register_6 (.D(I2), .en(Load), .clk(Clock), .Q(B2), .clr(RST));
  Register #(.width(1)) register_7 (.D(I1), .en(Load), .clk(Clock), .Q(B1), .clr(RST));
  Register #(.width(1)) register_8 (.D(I0), .en(Load), .clk(Clock), .Q(B0), .clr(RST));
  assign O7 = En ? B7 : 1'bz;  // Controlled_Buffer controlled_buffer_1
  assign O6 = En ? B6 : 1'bz;  // Controlled_Buffer controlled_buffer_2
  assign O5 = En ? B5 : 1'bz;  // Controlled_Buffer controlled_buffer_3
  assign O4 = En ? B4 : 1'bz;  // Controlled_Buffer controlled_buffer_4
  assign O3 = En ? B3 : 1'bz;  // Controlled_Buffer controlled_buffer_5
  assign O2 = En ? B2 : 1'bz;  // Controlled_Buffer controlled_buffer_6
  assign O1 = En ? B1 : 1'bz;  // Controlled_Buffer controlled_buffer_7
  assign O0 = En ? B0 : 1'bz;  // Controlled_Buffer controlled_buffer_8
endmodule

module Reverser (
  input  E0,
  input  E1,
  input  E2,
  input  E3,
  input  E4,
  input  E5,
  input  E6,
  input  E7,
  output S7,
  output S6,
  output S5,
  output S4,
  output S3,
  output S2,
  output S1,
  output S0
);


  assign S0 = E7;
  assign S1 = E6;
  assign S2 = E5;
  assign S3 = E4;
  assign S4 = E3;
  assign S5 = E2;
  assign S6 = E1;
  assign S7 = E0;
endmodule

// ProgramCounter
module CPU_Counter (
  input  COut,
  input  CEnable,
  input  CWrite,
  input  CReset,
  input  Clock,
  input  I7,
  input  I6,
  input  I5,
  input  I4,
  input  I3,
  input  I2,
  input  I1,
  input  I0,
  output O7,
  output O6,
  output O5,
  output O4,
  output O3,
  output O2,
  output O1,
  output O0,
  output D7,
  output D6,
  output D5,
  output D4,
  output D3,
  output D2,
  output D1,
  output D0
);

  wire and_1_out, and_2_out, and_3_out, and_4_out, and_5_out, and_6_out, and_7_out, and_8_out, and_9_out,
       and_10_out, and_11_out, and_12_out, and_13_out, and_14_out, and_15_out, and_16_out, j_k_ff_2_qn,
       j_k_ff_3_qn, j_k_ff_4_qn, j_k_ff_5_qn, j_k_ff_6_qn, j_k_ff_7_qn, j_k_ff_8_qn, or_1_out, or_2_out,
       or_3_out, or_4_out, or_5_out, or_6_out, or_7_out, or_8_out;

  and and_1 (and_1_out, CWrite, I7, Clock);
  J_K_Flip_Flop j_k_ff_1 (
    .J(CEnable), .K(CEnable), .clk(j_k_ff_2_qn), .Q(D7), .preset(and_1_out), .reset(or_1_out));  // open: Qn
  or or_1 (or_1_out, CReset, and_2_out);
  and and_2 (and_2_out, CWrite, ~I7, Clock);  // AND_Gate
  J_K_Flip_Flop j_k_ff_2 (
    .J(CEnable), .K(CEnable), .clk(j_k_ff_3_qn), .Q(D6), .Qn(j_k_ff_2_qn), .preset(and_3_out),
    .reset(or_2_out));
  or or_2 (or_2_out, CReset, and_4_out);
  and and_3 (and_3_out, CWrite, I6, Clock);
  and and_4 (and_4_out, CWrite, ~I6, Clock);  // AND_Gate
  J_K_Flip_Flop j_k_ff_3 (
    .J(CEnable), .K(CEnable), .clk(j_k_ff_4_qn), .Q(D5), .Qn(j_k_ff_3_qn), .preset(and_5_out),
    .reset(or_3_out));
  and and_5 (and_5_out, CWrite, I5, Clock);
  assign O7 = COut ? D7 : 1'bz;  // Controlled_Buffer controlled_buffer_1
  assign O6 = COut ? D6 : 1'bz;  // Controlled_Buffer controlled_buffer_2
  assign O5 = COut ? D5 : 1'bz;  // Controlled_Buffer controlled_buffer_3
  or or_3 (or_3_out, CReset, and_6_out);
  and and_6 (and_6_out, CWrite, ~I5, Clock);  // AND_Gate
  assign O4 = COut ? D4 : 1'bz;  // Controlled_Buffer controlled_buffer_4
  assign O3 = COut ? D3 : 1'bz;  // Controlled_Buffer controlled_buffer_5
  assign O2 = COut ? D2 : 1'bz;  // Controlled_Buffer controlled_buffer_6
  assign O1 = COut ? D1 : 1'bz;  // Controlled_Buffer controlled_buffer_7
  J_K_Flip_Flop j_k_ff_4 (
    .J(CEnable), .K(CEnable), .clk(j_k_ff_5_qn), .Q(D4), .Qn(j_k_ff_4_qn), .preset(and_7_out),
    .reset(or_4_out));
  or or_4 (or_4_out, CReset, and_8_out);
  and and_7 (and_7_out, CWrite, I4, Clock);
  and and_8 (and_8_out, CWrite, ~I4, Clock);  // AND_Gate
  assign O0 = COut ? D0 : 1'bz;  // Controlled_Buffer controlled_buffer_8
  J_K_Flip_Flop j_k_ff_5 (
    .J(CEnable), .K(CEnable), .clk(j_k_ff_6_qn), .Q(D3), .Qn(j_k_ff_5_qn), .preset(and_9_out),
    .reset(or_5_out));
  or or_5 (or_5_out, CReset, and_10_out);
  and and_9 (and_9_out, CWrite, I3, Clock);
  and and_10 (and_10_out, CWrite, ~I3, Clock);  // AND_Gate
  J_K_Flip_Flop j_k_ff_6 (
    .J(CEnable), .K(CEnable), .clk(j_k_ff_7_qn), .Q(D2), .Qn(j_k_ff_6_qn), .preset(and_11_out),
    .reset(or_6_out));
  and and_11 (and_11_out, CWrite, I2, Clock);
  or or_6 (or_6_out, CReset, and_12_out);
  and and_12 (and_12_out, CWrite, ~I2, Clock);  // AND_Gate
  J_K_Flip_Flop j_k_ff_7 (
    .J(CEnable), .K(CEnable), .clk(j_k_ff_8_qn), .Q(D1), .Qn(j_k_ff_7_qn), .preset(and_13_out),
    .reset(or_7_out));
  or or_7 (or_7_out, CReset, and_14_out);
  and and_13 (and_13_out, CWrite, I1, Clock);
  and and_14 (and_14_out, CWrite, ~I1, Clock);  // AND_Gate
  J_K_Flip_Flop j_k_ff_8 (
    .J(CEnable), .K(CEnable), .clk(Clock), .Q(D0), .Qn(j_k_ff_8_qn), .preset(and_15_out), .reset(or_8_out));
  or or_8 (or_8_out, CReset, and_16_out);
  and and_15 (and_15_out, CWrite, I0, Clock);
  and and_16 (and_16_out, CWrite, ~I0, Clock);  // AND_Gate
endmodule

module Address_Decoder (
  input  Enable,
  input  A3,
  input  A2,
  input  A1,
  input  A0,
  output DF,
  output DE,
  output DD,
  output DC,
  output DB,
  output DA,
  output D9,
  output D8,
  output D7,
  output D6,
  output D5,
  output D4,
  output D3,
  output D2,
  output D1,
  output D0
);

  wire and_1_out, and_2_out, and_3_out, and_4_out, and_5_out, and_6_out, and_7_out, and_8_out, and_9_out,
       and_10_out, and_11_out, and_12_out, and_13_out, and_14_out, and_15_out, and_16_out, not_1_out,
       not_2_out, not_3_out, not_4_out;

  not not_1 (not_1_out, A3);
  not not_2 (not_2_out, A2);
  not not_3 (not_3_out, A1);
  not not_4 (not_4_out, A0);
  and and_1 (and_1_out, not_1_out, not_2_out, not_3_out, not_4_out);
  and and_2 (and_2_out, not_1_out, not_2_out, not_3_out, A0);
  and and_3 (and_3_out, not_1_out, not_2_out, A1, not_4_out);
  and and_4 (and_4_out, not_1_out, not_2_out, A1, A0);
  and and_5 (and_5_out, not_1_out, A2, not_3_out, not_4_out);
  and and_6 (and_6_out, not_1_out, A2, not_3_out, A0);
  and and_7 (and_7_out, not_1_out, A2, A1, not_4_out);
  and and_8 (and_8_out, not_1_out, A2, A1, A0);
  and and_9 (and_9_out, A3, not_2_out, not_3_out, not_4_out);
  and and_10 (and_10_out, A3, not_2_out, not_3_out, A0);
  and and_11 (and_11_out, A3, not_2_out, A1, not_4_out);
  and and_12 (and_12_out, A3, not_2_out, A1, A0);
  and and_13 (and_13_out, A3, A2, not_3_out, not_4_out);
  and and_14 (and_14_out, A3, A2, not_3_out, A0);
  and and_15 (and_15_out, A3, A2, A1, not_4_out);
  and and_16 (and_16_out, A3, A2, A1, A0);
  assign DF = Enable ? and_16_out : 1'bz;  // Controlled_Buffer controlled_buffer_1
  assign DE = Enable ? and_15_out : 1'bz;  // Controlled_Buffer controlled_buffer_2
  assign DD = Enable ? and_14_out : 1'bz;  // Controlled_Buffer controlled_buffer_3
  assign DC = Enable ? and_13_out : 1'bz;  // Controlled_Buffer controlled_buffer_4
  assign DB = Enable ? and_12_out : 1'bz;  // Controlled_Buffer controlled_buffer_5
  assign DA = Enable ? and_11_out : 1'bz;  // Controlled_Buffer controlled_buffer_6
  assign D9 = Enable ? and_10_out : 1'bz;  // Controlled_Buffer controlled_buffer_7
  assign D8 = Enable ? and_9_out : 1'bz;  // Controlled_Buffer controlled_buffer_8
  assign D7 = Enable ? and_8_out : 1'bz;  // Controlled_Buffer controlled_buffer_9
  assign D6 = Enable ? and_7_out : 1'bz;  // Controlled_Buffer controlled_buffer_10
  assign D5 = Enable ? and_6_out : 1'bz;  // Controlled_Buffer controlled_buffer_11
  assign D4 = Enable ? and_5_out : 1'bz;  // Controlled_Buffer controlled_buffer_12
  assign D3 = Enable ? and_4_out : 1'bz;  // Controlled_Buffer controlled_buffer_13
  assign D2 = Enable ? and_3_out : 1'bz;  // Controlled_Buffer controlled_buffer_14
  assign D1 = Enable ? and_2_out : 1'bz;  // Controlled_Buffer controlled_buffer_15
  assign D0 = Enable ? and_1_out : 1'bz;  // Controlled_Buffer controlled_buffer_16
endmodule

module Program_Loader (
  input  [7:0] ROM_Data,
  input  Reset,
  input  Enable,
  input  Clock,
  output [7:0] ROM_Addr,
  output O7,
  output O6,
  output O5,
  output O4,
  output O3,
  output O2,
  output O1,
  output O0,
  output Programming,
  output Addr_Write,
  output RAM_Write
);

  wire j_k_ff_1_q, j_k_ff_1_qn;
  wire [7:0] controlled_buffer_1_out;

  CPU_Counter Counter (
    .COut(Enable), .CEnable(Enable), .CWrite(1'b0), .CReset(Reset), .Clock(j_k_ff_1_qn), .O7(ROM_Addr[7]),
    .O6(ROM_Addr[6]), .O5(ROM_Addr[5]), .O4(ROM_Addr[4]), .O3(ROM_Addr[3]), .O2(ROM_Addr[2]),
    .O1(ROM_Addr[1]), .O0(ROM_Addr[0]));  // open: I7, I6, I5, I4, I3, I2, I1, I0, D7, D6, D5, D4, D3, D2, D1, D0
  assign controlled_buffer_1_out = j_k_ff_1_qn ? ROM_Addr : 8'bz;  // Controlled_Buffer controlled_buffer_1
  assign controlled_buffer_1_out = j_k_ff_1_q ? ROM_Data : 8'bz;  // Controlled_Buffer controlled_buffer_2
  J_K_Flip_Flop j_k_ff_1 (
    .J(Clock), .K(Clock), .clk(Clock), .Q(j_k_ff_1_q), .Qn(j_k_ff_1_qn), .preset(1'b0), .reset(1'b0));
  assign O7 = Enable ? controlled_buffer_1_out[7] : 1'bz;  // Controlled_Buffer controlled_buffer_3
  assign O6 = Enable ? controlled_buffer_1_out[6] : 1'bz;  // Controlled_Buffer controlled_buffer_4
  assign O5 = Enable ? controlled_buffer_1_out[5] : 1'bz;  // Controlled_Buffer controlled_buffer_5
  assign O4 = Enable ? controlled_buffer_1_out[4] : 1'bz;  // Controlled_Buffer controlled_buffer_6
  assign O3 = Enable ? controlled_buffer_1_out[3] : 1'bz;  // Controlled_Buffer controlled_buffer_7
  assign O2 = Enable ? controlled_buffer_1_out[2] : 1'bz;  // Controlled_Buffer controlled_buffer_8
  assign O1 = Enable ? controlled_buffer_1_out[1] : 1'bz;  // Controlled_Buffer controlled_buffer_9
  assign O0 = Enable ? controlled_buffer_1_out[0] : 1'bz;  // Controlled_Buffer controlled_buffer_10
  and and_1 (Addr_Write, j_k_ff_1_qn, Enable);
  and and_2 (RAM_Write, j_k_ff_1_q, Enable);

  assign Programming = Enable;
endmodule

module Instruction_Decoder (
  input  Programming_Mode,
  input  ZF,
  input  CF,
  input  CS0,
  input  CS1,
  input  CS2,
  input  CS3,
  input  CS4,
  input  CS5,
  input  Clear,
  input  Clock,
  output ALU_S0,
  output ALU_S1,
  output ALU_S2,
  output JP,
  output C_out,
  output C_en,
  output IR_res,
  output IR_in,
  output RR,
  output RW,
  output MAR_in,
  output RD_out,
  output RD_in,
  output RC_out,
  output RC_in,
  output RB_out,
  output RB_in,
  output RA_out,
  output RA_in,
  output Disp,
  output ALU_out,
  output Flags_in,
  output Halt,
  output S7,
  output S6,
  output S5,
  output S4,
  output S3,
  output S2,
  output S1,
  output S0
);

  wire address_decoder_1_d8, cpu_counter_1_o3, not_1_out, not_2_out, or_1_out;
  wire [2:0] cpu_counter_1_o0;
  wire [23:0] rom_1_data;

  not not_1 (not_1_out, Clock);
  or or_1 (or_1_out, Clear, rom_1_data[7], address_decoder_1_d8);
  CPU_Counter cpu_counter_1 (
    .COut(1'b1), .CEnable(1'b1), .CWrite(1'b0), .CReset(or_1_out), .Clock(not_1_out), .O3(cpu_counter_1_o3),
    .O2(cpu_counter_1_o0[2]), .O1(cpu_counter_1_o0[1]), .O0(cpu_counter_1_o0[0]));  // open: I7, I6, I5, I4, I3, I2, I1, I0, O7, O6, O5, O4, D7, D6, D5, D4, D3, D2, D1, D0
  Address_Decoder address_decoder_1 (
    .Enable(1'b1), .A3(cpu_counter_1_o3), .A2(cpu_counter_1_o0[2]), .A1(cpu_counter_1_o0[1]),
    .A0(cpu_counter_1_o0[0]), .D8(address_decoder_1_d8), .D7(S7), .D6(S6), .D5(S5), .D4(S4), .D3(S3),
    .D2(S2), .D1(S1), .D0(S0));  // open: DF, DE, DD, DC, DB, DA, D9
  ROM #(.addrWidth(11), .dataWidth(24)) rom_1 (
    .addr({CS5, CS4, CS3, CS2, CS1, CS0, CF, ZF, cpu_counter_1_o0}), .data(rom_1_data));
  not not_2 (not_2_out, Programming_Mode);
  // NoConnect on rom_1_data[0]
  and and_1 (ALU_S0, not_2_out, rom_1_data[1]);
  and and_2 (ALU_S1, not_2_out, rom_1_data[2]);
  and and_3 (ALU_S2, not_2_out, rom_1_data[3]);
  and and_4 (JP, not_2_out, rom_1_data[4]);
  and and_5 (C_out, not_2_out, rom_1_data[5]);
  and and_6 (C_en, not_2_out, rom_1_data[6]);
  and and_7 (IR_res, not_2_out, rom_1_data[7]);
  and and_8 (IR_in, not_2_out, rom_1_data[8]);
  and and_9 (RR, not_2_out, rom_1_data[9]);
  and and_10 (RW, not_2_out, rom_1_data[10]);
  and and_11 (MAR_in, not_2_out, rom_1_data[11]);
  and and_12 (RD_out, not_2_out, rom_1_data[12]);
  and and_13 (RD_in, not_2_out, rom_1_data[13]);
  and and_14 (RC_out, not_2_out, rom_1_data[14]);
  and and_15 (RC_in, not_2_out, rom_1_data[15]);
  and and_16 (RB_out, not_2_out, rom_1_data[16]);
  and and_17 (RB_in, not_2_out, rom_1_data[17]);
  and and_18 (RA_out, not_2_out, rom_1_data[18]);
  and and_19 (RA_in, not_2_out, rom_1_data[19]);
  and and_20 (Disp, not_2_out, rom_1_data[20]);
  and and_21 (ALU_out, not_2_out, rom_1_data[21]);
  and and_22 (Flags_in, not_2_out, rom_1_data[22]);
  and and_23 (Halt, not_2_out, rom_1_data[23]);

  // Notes on the sheet:
  //   contents of rom_1 (hex, n*v repeats v):
  //   820 340 80 5*0 820 340 80 5*0 820 340 80 5*0 820 340 80 5*0 820 340 800000 80 4*0 820 340 800000 80
  //   4*0 820 340 800000 80 4*0 820 340 800000 80 4*0 820 340 860 80200 80 0 0 0 820 340 860 80200 80 0 0
  //   0 820 340 860 80200 80 0 0 0 820 340 860 80200 80 0 0 0 820 340 860 a00 80200 80 0 0 820 340 860 a00
  //   80200 80 0 0 820 340 860 a00 80200 80 0 0 820 340 860 a00 80200 80 0 0 820 340 860 a00 40400 80 0 0
  //   820 340 860 a00 40400 80 0 0 820 340 860 a00 40400 80 0 0 820 340 860 a00 40400 80 0 0 820 340 860
  //   20200 80 0 0 0 820 340 860 20200 80 0 0 0 820 340 860 20200 80 0 0 0 820 340 860 20200 80 0 0 0 820
  //   340 860 a40 20200 80 0 0 820 340 860 a40 20200 80 0 0 820 340 860 a40 20200 80 0 0 820 340 860 a40
  //   20200 80 0 0 820 340 860 a00 10400 80 0 0 820 340 860 a00 10400 80 0 0 820 340 860 a00 10400 80 0 0
  //   820 340 860 a00 10400 80 0 0 820 340 860 20200 680000 80 0 0 820 340 860 20200 680000 80 0 0 820 340
  //   860 20200 680000 80 0 0 820 340 860 20200 680000 80 0 0 820 340 860 680000 80 0 0 0 820 340 860
  //   680000 80 0 0 0 820 340 860 680000 80 0 0 0 820 340 860 680000 80 0 0 0 820 340 860 20202 680002 80
  //   0 0 820 340 860 20202 680002 80 0 0 820 340 860 20202 680002 80 0 0 820 340 860 20202 680002 80 0 0
  //   820 340 860 680000 80 0 0 0 820 340 860 680000 80 0 0 0 820 340 860 680000 80 0 0 0 820 340 860
  //   680000 80 0 0 0 820 340 860 84000 80 0 0 0 820 340 860 84000 80 0 0 0 820 340 860 84000 80 0 0 0 820
  //   340 860 84000 80 0 0 0 820 340 860 48000 80 0 0 0 820 340 860 48000 80 0 0 0 820 340 860 48000 80 0
  //   0 0 820 340 860 48000 80 0 0 0 820 340 860 81000 80 0 0 0 820 340 860 81000 80 0 0 0 820 340 860
  //   81000 80 0 0 0 820 340 860 81000 80 0 0 0 820 340 860 42000 80 0 0 0 820 340 860 42000 80 0 0 0 820
  //   340 860 42000 80 0 0 0 820 340 860 42000 80 0 0 0 820 340 860 24000 80 0 0 0 820 340 860 24000 80 0
  //   0 0 820 340 860 24000 80 0 0 0 820 340 860 24000 80 0 0 0 820 340 860 18000 80 0 0 0 820 340 860
  //   18000 80 0 0 0 820 340 860 18000 80 0 0 0 820 340 860 18000 80 0 0 0 820 340 860 21000 80 0 0 0 820
  //   340 860 21000 80 0 0 0 820 340 860 21000 80 0 0 0 820 340 860 21000 80 0 0 0 820 340 860 12000 80 0
  //   0 0 820 340 860 12000 80 0 0 0 820 340 860 12000 80 0 0 0 820 340 860 12000 80 0 0 0 820 340 860 210
  //   80 0 0 0 820 340 860 210 80 0 0 0 820 340 860 210 80 0 0 0 820 340 860 210 80 0 0 0 820 340 40 80
  //   4*0 820 340 40 80 4*0 820 340 40 80 4*0 820 340 40 80 4*0 820 340 860 210 80 0 0 0 820 340 860 210
  //   80 0 0 0 820 340 860 210 80 0 0 0 820 340 860 210 80 0 0 0 820 340 40 80 4*0 820 340 40 80 4*0 820
  //   340 40 80 4*0 820 340 40 80 4*0 820 340 860 210 80 0 0 0 820 340 860 210 80 0 0 0 820 340 860 210 80
  //   0 0 0 820 340 860 210 80 0 0 0 820 340 860 8200 80 0 0 0 820 340 860 8200 80 0 0 0 820 340 860 8200
  //   80 0 0 0 820 340 860 8200 80 0 0 0 820 340 860 2200 80 0 0 0 820 340 860 2200 80 0 0 0 820 340 860
  //   2200 80 0 0 0 820 340 860 2200 80 0 0 0 820 340 860 680004 80 0 0 0 820 340 860 680004 80 0 0 0 820
  //   340 860 680004 80 0 0 0 820 340 860 680004 80 0 0 0 820 340 860 680006 80 0 0 0 820 340 860 680006
  //   80 0 0 0 820 340 860 680006 80 0 0 0 820 340 860 680006 80 0 0 0 820 340 860 680008 80 0 0 0 820 340
  //   860 680008 80 0 0 0 820 340 860 680008 80 0 0 0 820 340 860 680008 80 0 0 0 820 340 860 68000a 80 0
  //   0 0 820 340 860 68000a 80 0 0 0 820 340 860 68000a 80 0 0 0 820 340 860 68000a 80 0 0 0 820 340
  //   140000 80 4*0 820 340 140000 80 4*0 820 340 140000 80 4*0 820 340 140000 80
endmodule

module Reg_2bit (
  input  Clock,
  input  Load,
  input  Rst,
  input  En,
  input  I1,
  input  I0,
  output B1,
  output B0,
  output O1,
  output O0
);

  Register #(.width(1)) register_1 (.D(I1), .en(Load), .clk(Clock), .Q(B1), .clr(Rst));
  Register #(.width(1)) register_2 (.D(I0), .en(Load), .clk(Clock), .Q(B0), .clr(Rst));
  assign O1 = En ? B1 : 1'bz;  // Controlled_Buffer controlled_buffer_1
  assign O0 = En ? B0 : 1'bz;  // Controlled_Buffer controlled_buffer_2
endmodule

module Address_Decoder_4_bits (
  input  A3,
  input  Enable,
  input  A2,
  input  A1,
  input  A0,
  output DF,
  output DE,
  output DD,
  output DC,
  output DB,
  output DA,
  output D9,
  output D8,
  output D7,
  output D6,
  output D5,
  output D4,
  output D3,
  output D2,
  output D1,
  output D0
);

  wire and_1_out, and_2_out, and_3_out, and_4_out, and_5_out, and_6_out, and_7_out, and_8_out, and_9_out,
       and_10_out, and_11_out, and_12_out, and_13_out, and_14_out, and_15_out, and_16_out, not_1_out,
       not_2_out, not_3_out, not_4_out;

  not not_1 (not_1_out, A3);
  not not_2 (not_2_out, A2);
  not not_3 (not_3_out, A1);
  not not_4 (not_4_out, A0);
  assign DF = Enable ? and_16_out : 1'bz;  // Controlled_Buffer controlled_buffer_1
  assign DE = Enable ? and_15_out : 1'bz;  // Controlled_Buffer controlled_buffer_2
  and and_1 (and_1_out, not_1_out, not_2_out, not_3_out, not_4_out);
  and and_2 (and_2_out, not_1_out, not_2_out, not_3_out, A0);
  and and_3 (and_3_out, not_1_out, not_2_out, A1, not_4_out);
  and and_4 (and_4_out, not_1_out, not_2_out, A1, A0);
  and and_5 (and_5_out, not_1_out, A2, not_3_out, not_4_out);
  and and_6 (and_6_out, not_1_out, A2, not_3_out, A0);
  and and_7 (and_7_out, not_1_out, A2, A1, not_4_out);
  and and_8 (and_8_out, not_1_out, A2, A1, A0);
  and and_9 (and_9_out, A3, not_2_out, not_3_out, not_4_out);
  and and_10 (and_10_out, A3, not_2_out, not_3_out, A0);
  and and_11 (and_11_out, A3, not_2_out, A1, not_4_out);
  and and_12 (and_12_out, A3, not_2_out, A1, A0);
  and and_13 (and_13_out, A3, A2, not_3_out, not_4_out);
  and and_14 (and_14_out, A3, A2, not_3_out, A0);
  and and_15 (and_15_out, A3, A2, A1, not_4_out);
  and and_16 (and_16_out, A3, A2, A1, A0);
  assign DD = Enable ? and_14_out : 1'bz;  // Controlled_Buffer controlled_buffer_3
  assign DC = Enable ? and_13_out : 1'bz;  // Controlled_Buffer controlled_buffer_4
  assign DB = Enable ? and_12_out : 1'bz;  // Controlled_Buffer controlled_buffer_5
  assign DA = Enable ? and_11_out : 1'bz;  // Controlled_Buffer controlled_buffer_6
  assign D9 = Enable ? and_10_out : 1'bz;  // Controlled_Buffer controlled_buffer_7
  assign D8 = Enable ? and_9_out : 1'bz;  // Controlled_Buffer controlled_buffer_8
  assign D7 = Enable ? and_8_out : 1'bz;  // Controlled_Buffer controlled_buffer_9
  assign D6 = Enable ? and_7_out : 1'bz;  // Controlled_Buffer controlled_buffer_10
  assign D5 = Enable ? and_6_out : 1'bz;  // Controlled_Buffer controlled_buffer_11
  assign D4 = Enable ? and_5_out : 1'bz;  // Controlled_Buffer controlled_buffer_12
  assign D3 = Enable ? and_4_out : 1'bz;  // Controlled_Buffer controlled_buffer_13
  assign D2 = Enable ? and_3_out : 1'bz;  // Controlled_Buffer controlled_buffer_14
  assign D1 = Enable ? and_2_out : 1'bz;  // Controlled_Buffer controlled_buffer_15
  assign D0 = Enable ? and_1_out : 1'bz;  // Controlled_Buffer controlled_buffer_16
endmodule

module SRAM_16_bytes (
  input  I7,
  input  I6,
  input  I5,
  input  I4,
  input  I3,
  input  I2,
  input  I1,
  input  I0,
  input  Read,
  input  Write,
  input  Clear,
  input  Clock,
  input  A3,
  input  A2,
  input  A1,
  input  A0,
  output D7,
  output D6,
  output D5,
  output D4,
  output D3,
  output D2,
  output D1,
  output D0,
  output O7,
  output O6,
  output O5,
  output O4,
  output O3,
  output O2,
  output O1,
  output O0
);

  wire address_decoder_4_bits_1_d0, address_decoder_4_bits_1_d1, address_decoder_4_bits_1_d2,
       address_decoder_4_bits_1_d3, address_decoder_4_bits_1_d4, address_decoder_4_bits_1_d5,
       address_decoder_4_bits_1_d6, address_decoder_4_bits_1_d7, address_decoder_4_bits_1_d8,
       address_decoder_4_bits_1_d9, address_decoder_4_bits_1_da, address_decoder_4_bits_1_db,
       address_decoder_4_bits_1_dc, address_decoder_4_bits_1_dd, address_decoder_4_bits_1_de,
       address_decoder_4_bits_1_df, and_1_out, and_2_out, and_3_out, and_4_out, and_5_out, and_6_out,
       and_7_out, and_8_out, and_9_out, and_10_out, and_11_out, and_12_out, and_13_out, and_14_out,
       and_15_out, and_16_out, controlled_buffer_9_out, controlled_buffer_10_out, controlled_buffer_11_out,
       controlled_buffer_12_out, controlled_buffer_13_out, controlled_buffer_14_out,
       controlled_buffer_15_out, controlled_buffer_16_out, reg_8bit_1_b0, reg_8bit_1_b1, reg_8bit_1_b2,
       reg_8bit_1_b3, reg_8bit_1_b4, reg_8bit_1_b5, reg_8bit_1_b6, reg_8bit_1_b7, reg_8bit_2_b0,
       reg_8bit_2_b1, reg_8bit_2_b2, reg_8bit_2_b3, reg_8bit_2_b4, reg_8bit_2_b5, reg_8bit_2_b6,
       reg_8bit_2_b7, reg_8bit_3_b0, reg_8bit_3_b1, reg_8bit_3_b2, reg_8bit_3_b3, reg_8bit_3_b4,
       reg_8bit_3_b5, reg_8bit_3_b6, reg_8bit_3_b7, reg_8bit_4_b0, reg_8bit_4_b1, reg_8bit_4_b2,
       reg_8bit_4_b3, reg_8bit_4_b4, reg_8bit_4_b5, reg_8bit_4_b6, reg_8bit_4_b7, reg_8bit_5_b0,
       reg_8bit_5_b1, reg_8bit_5_b2, reg_8bit_5_b3, reg_8bit_5_b4, reg_8bit_5_b5, reg_8bit_5_b6,
       reg_8bit_5_b7, reg_8bit_6_b0, reg_8bit_6_b1, reg_8bit_6_b2, reg_8bit_6_b3, reg_8bit_6_b4,
       reg_8bit_6_b5, reg_8bit_6_b6, reg_8bit_6_b7, reg_8bit_7_b0, reg_8bit_7_b1, reg_8bit_7_b2,
       reg_8bit_7_b3, reg_8bit_7_b4, reg_8bit_7_b5, reg_8bit_7_b6, reg_8bit_7_b7, reg_8bit_8_b0,
       reg_8bit_8_b1, reg_8bit_8_b2, reg_8bit_8_b3, reg_8bit_8_b4, reg_8bit_8_b5, reg_8bit_8_b6,
       reg_8bit_8_b7, reg_8bit_9_b0, reg_8bit_9_b1, reg_8bit_9_b2, reg_8bit_9_b3, reg_8bit_9_b4,
       reg_8bit_9_b5, reg_8bit_9_b6, reg_8bit_9_b7, reg_8bit_10_b0, reg_8bit_10_b1, reg_8bit_10_b2,
       reg_8bit_10_b3, reg_8bit_10_b4, reg_8bit_10_b5, reg_8bit_10_b6, reg_8bit_10_b7, reg_8bit_11_b0,
       reg_8bit_11_b1, reg_8bit_11_b2, reg_8bit_11_b3, reg_8bit_11_b4, reg_8bit_11_b5, reg_8bit_11_b6,
       reg_8bit_11_b7, reg_8bit_12_b0, reg_8bit_12_b1, reg_8bit_12_b2, reg_8bit_12_b3, reg_8bit_12_b4,
       reg_8bit_12_b5, reg_8bit_12_b6, reg_8bit_12_b7, reg_8bit_13_b0, reg_8bit_13_b1, reg_8bit_13_b2,
       reg_8bit_13_b3, reg_8bit_13_b4, reg_8bit_13_b5, reg_8bit_13_b6, reg_8bit_13_b7, reg_8bit_14_b0,
       reg_8bit_14_b1, reg_8bit_14_b2, reg_8bit_14_b3, reg_8bit_14_b4, reg_8bit_14_b5, reg_8bit_14_b6,
       reg_8bit_14_b7, reg_8bit_15_b0, reg_8bit_15_b1, reg_8bit_15_b2, reg_8bit_15_b3, reg_8bit_15_b4,
       reg_8bit_15_b5, reg_8bit_15_b6, reg_8bit_15_b7, reg_8bit_16_b0, reg_8bit_16_b1, reg_8bit_16_b2,
       reg_8bit_16_b3, reg_8bit_16_b4, reg_8bit_16_b5, reg_8bit_16_b6, reg_8bit_16_b7;

  Address_Decoder_4_bits address_decoder_4_bits_1 (
    .Enable(1'b1), .A1(A1), .A0(A0), .A3(A3), .A2(A2), .DF(address_decoder_4_bits_1_df),
    .DE(address_decoder_4_bits_1_de), .DD(address_decoder_4_bits_1_dd), .DC(address_decoder_4_bits_1_dc),
    .DB(address_decoder_4_bits_1_db), .DA(address_decoder_4_bits_1_da), .D9(address_decoder_4_bits_1_d9),
    .D8(address_decoder_4_bits_1_d8), .D7(address_decoder_4_bits_1_d7), .D6(address_decoder_4_bits_1_d6),
    .D5(address_decoder_4_bits_1_d5), .D4(address_decoder_4_bits_1_d4), .D3(address_decoder_4_bits_1_d3),
    .D2(address_decoder_4_bits_1_d2), .D1(address_decoder_4_bits_1_d1), .D0(address_decoder_4_bits_1_d0));
  DotMatrix #(.dotshape("circle"), .inputtype("row"), .matrixcols(1), .matrixrows(8)) dotmatrix_1 (
    .row0(reg_8bit_1_b7), .row1(reg_8bit_1_b6), .row2(reg_8bit_1_b5), .row3(reg_8bit_1_b4),
    .row4(reg_8bit_1_b3), .row5(reg_8bit_1_b2), .row6(reg_8bit_1_b1), .row7(reg_8bit_1_b0));
  DotMatrix #(.dotshape("circle"), .inputtype("row"), .matrixcols(1), .matrixrows(8)) dotmatrix_2 (
    .row0(reg_8bit_2_b7), .row1(reg_8bit_2_b6), .row2(reg_8bit_2_b5), .row3(reg_8bit_2_b4),
    .row4(reg_8bit_2_b3), .row5(reg_8bit_2_b2), .row6(reg_8bit_2_b1), .row7(reg_8bit_2_b0));
  DotMatrix #(.dotshape("circle"), .inputtype("row"), .matrixcols(1), .matrixrows(8)) dotmatrix_3 (
    .row0(reg_8bit_3_b7), .row1(reg_8bit_3_b6), .row2(reg_8bit_3_b5), .row3(reg_8bit_3_b4),
    .row4(reg_8bit_3_b3), .row5(reg_8bit_3_b2), .row6(reg_8bit_3_b1), .row7(reg_8bit_3_b0));
  DotMatrix #(.dotshape("circle"), .inputtype("row"), .matrixcols(1), .matrixrows(8)) dotmatrix_4 (
    .row0(reg_8bit_4_b7), .row1(reg_8bit_4_b6), .row2(reg_8bit_4_b5), .row3(reg_8bit_4_b4),
    .row4(reg_8bit_4_b3), .row5(reg_8bit_4_b2), .row6(reg_8bit_4_b1), .row7(reg_8bit_4_b0));
  DotMatrix #(.dotshape("circle"), .inputtype("row"), .matrixcols(1), .matrixrows(8)) dotmatrix_5 (
    .row0(reg_8bit_5_b7), .row1(reg_8bit_5_b6), .row2(reg_8bit_5_b5), .row3(reg_8bit_5_b4),
    .row4(reg_8bit_5_b3), .row5(reg_8bit_5_b2), .row6(reg_8bit_5_b1), .row7(reg_8bit_5_b0));
  DotMatrix #(.dotshape("circle"), .inputtype("row"), .matrixcols(1), .matrixrows(8)) dotmatrix_6 (
    .row0(reg_8bit_6_b7), .row1(reg_8bit_6_b6), .row2(reg_8bit_6_b5), .row3(reg_8bit_6_b4),
    .row4(reg_8bit_6_b3), .row5(reg_8bit_6_b2), .row6(reg_8bit_6_b1), .row7(reg_8bit_6_b0));
  DotMatrix #(.dotshape("circle"), .inputtype("row"), .matrixcols(1), .matrixrows(8)) dotmatrix_7 (
    .row0(reg_8bit_7_b7), .row1(reg_8bit_7_b6), .row2(reg_8bit_7_b5), .row3(reg_8bit_7_b4),
    .row4(reg_8bit_7_b3), .row5(reg_8bit_7_b2), .row6(reg_8bit_7_b1), .row7(reg_8bit_7_b0));
  DotMatrix #(.dotshape("circle"), .inputtype("row"), .matrixcols(1), .matrixrows(8)) dotmatrix_8 (
    .row0(reg_8bit_8_b7), .row1(reg_8bit_8_b6), .row2(reg_8bit_8_b5), .row3(reg_8bit_8_b4),
    .row4(reg_8bit_8_b3), .row5(reg_8bit_8_b2), .row6(reg_8bit_8_b1), .row7(reg_8bit_8_b0));
  assign O7 = Read ? D7 : 1'bz;  // Controlled_Buffer controlled_buffer_1
  Reg_8bit reg_8bit_1 (
    .I7(controlled_buffer_9_out), .I6(controlled_buffer_10_out), .I5(controlled_buffer_11_out),
    .I4(controlled_buffer_12_out), .I3(controlled_buffer_13_out), .I2(controlled_buffer_14_out),
    .I1(controlled_buffer_15_out), .I0(controlled_buffer_16_out), .Clock(Clock), .Load(and_1_out),
    .RST(Clear), .En(address_decoder_4_bits_1_df), .O7(D7), .O6(D6), .O5(D5), .O4(D4), .O3(D3), .O2(D2),
    .O1(D1), .O0(D0), .B7(reg_8bit_1_b7), .B6(reg_8bit_1_b6), .B5(reg_8bit_1_b5), .B4(reg_8bit_1_b4),
    .B3(reg_8bit_1_b3), .B2(reg_8bit_1_b2), .B1(reg_8bit_1_b1), .B0(reg_8bit_1_b0));
  Reg_8bit reg_8bit_2 (
    .I7(controlled_buffer_9_out), .I6(controlled_buffer_10_out), .I5(controlled_buffer_11_out),
    .I4(controlled_buffer_12_out), .I3(controlled_buffer_13_out), .I2(controlled_buffer_14_out),
    .I1(controlled_buffer_15_out), .I0(controlled_buffer_16_out), .Clock(Clock), .Load(and_2_out),
    .RST(Clear), .En(address_decoder_4_bits_1_de), .O7(D7), .O6(D6), .O5(D5), .O4(D4), .O3(D3), .O2(D2),
    .O1(D1), .O0(D0), .B7(reg_8bit_2_b7), .B6(reg_8bit_2_b6), .B5(reg_8bit_2_b5), .B4(reg_8bit_2_b4),
    .B3(reg_8bit_2_b3), .B2(reg_8bit_2_b2), .B1(reg_8bit_2_b1), .B0(reg_8bit_2_b0));
  Reg_8bit reg_8bit_3 (
    .I7(controlled_buffer_9_out), .I6(controlled_buffer_10_out), .I5(controlled_buffer_11_out),
    .I4(controlled_buffer_12_out), .I3(controlled_buffer_13_out), .I2(controlled_buffer_14_out),
    .I1(controlled_buffer_15_out), .I0(controlled_buffer_16_out), .Clock(Clock), .Load(and_3_out),
    .RST(Clear), .En(address_decoder_4_bits_1_dd), .O7(D7), .O6(D6), .O5(D5), .O4(D4), .O3(D3), .O2(D2),
    .O1(D1), .O0(D0), .B7(reg_8bit_3_b7), .B6(reg_8bit_3_b6), .B5(reg_8bit_3_b5), .B4(reg_8bit_3_b4),
    .B3(reg_8bit_3_b3), .B2(reg_8bit_3_b2), .B1(reg_8bit_3_b1), .B0(reg_8bit_3_b0));
  Reg_8bit reg_8bit_4 (
    .I7(controlled_buffer_9_out), .I6(controlled_buffer_10_out), .I5(controlled_buffer_11_out),
    .I4(controlled_buffer_12_out), .I3(controlled_buffer_13_out), .I2(controlled_buffer_14_out),
    .I1(controlled_buffer_15_out), .I0(controlled_buffer_16_out), .Clock(Clock), .Load(and_4_out),
    .RST(Clear), .En(address_decoder_4_bits_1_dc), .O7(D7), .O6(D6), .O5(D5), .O4(D4), .O3(D3), .O2(D2),
    .O1(D1), .O0(D0), .B7(reg_8bit_4_b7), .B6(reg_8bit_4_b6), .B5(reg_8bit_4_b5), .B4(reg_8bit_4_b4),
    .B3(reg_8bit_4_b3), .B2(reg_8bit_4_b2), .B1(reg_8bit_4_b1), .B0(reg_8bit_4_b0));
  Reg_8bit reg_8bit_5 (
    .I7(controlled_buffer_9_out), .I6(controlled_buffer_10_out), .I5(controlled_buffer_11_out),
    .I4(controlled_buffer_12_out), .I3(controlled_buffer_13_out), .I2(controlled_buffer_14_out),
    .I1(controlled_buffer_15_out), .I0(controlled_buffer_16_out), .Clock(Clock), .Load(and_5_out),
    .RST(Clear), .En(address_decoder_4_bits_1_db), .O7(D7), .O6(D6), .O5(D5), .O4(D4), .O3(D3), .O2(D2),
    .O1(D1), .O0(D0), .B7(reg_8bit_5_b7), .B6(reg_8bit_5_b6), .B5(reg_8bit_5_b5), .B4(reg_8bit_5_b4),
    .B3(reg_8bit_5_b3), .B2(reg_8bit_5_b2), .B1(reg_8bit_5_b1), .B0(reg_8bit_5_b0));
  Reg_8bit reg_8bit_6 (
    .I7(controlled_buffer_9_out), .I6(controlled_buffer_10_out), .I5(controlled_buffer_11_out),
    .I4(controlled_buffer_12_out), .I3(controlled_buffer_13_out), .I2(controlled_buffer_14_out),
    .I1(controlled_buffer_15_out), .I0(controlled_buffer_16_out), .Clock(Clock), .Load(and_6_out),
    .RST(Clear), .En(address_decoder_4_bits_1_da), .O7(D7), .O6(D6), .O5(D5), .O4(D4), .O3(D3), .O2(D2),
    .O1(D1), .O0(D0), .B7(reg_8bit_6_b7), .B6(reg_8bit_6_b6), .B5(reg_8bit_6_b5), .B4(reg_8bit_6_b4),
    .B3(reg_8bit_6_b3), .B2(reg_8bit_6_b2), .B1(reg_8bit_6_b1), .B0(reg_8bit_6_b0));
  Reg_8bit reg_8bit_7 (
    .I7(controlled_buffer_9_out), .I6(controlled_buffer_10_out), .I5(controlled_buffer_11_out),
    .I4(controlled_buffer_12_out), .I3(controlled_buffer_13_out), .I2(controlled_buffer_14_out),
    .I1(controlled_buffer_15_out), .I0(controlled_buffer_16_out), .Clock(Clock), .Load(and_7_out),
    .RST(Clear), .En(address_decoder_4_bits_1_d9), .O7(D7), .O6(D6), .O5(D5), .O4(D4), .O3(D3), .O2(D2),
    .O1(D1), .O0(D0), .B7(reg_8bit_7_b7), .B6(reg_8bit_7_b6), .B5(reg_8bit_7_b5), .B4(reg_8bit_7_b4),
    .B3(reg_8bit_7_b3), .B2(reg_8bit_7_b2), .B1(reg_8bit_7_b1), .B0(reg_8bit_7_b0));
  Reg_8bit reg_8bit_8 (
    .I7(controlled_buffer_9_out), .I6(controlled_buffer_10_out), .I5(controlled_buffer_11_out),
    .I4(controlled_buffer_12_out), .I3(controlled_buffer_13_out), .I2(controlled_buffer_14_out),
    .I1(controlled_buffer_15_out), .I0(controlled_buffer_16_out), .Clock(Clock), .Load(and_8_out),
    .RST(Clear), .En(address_decoder_4_bits_1_d8), .O7(D7), .O6(D6), .O5(D5), .O4(D4), .O3(D3), .O2(D2),
    .O1(D1), .O0(D0), .B7(reg_8bit_8_b7), .B6(reg_8bit_8_b6), .B5(reg_8bit_8_b5), .B4(reg_8bit_8_b4),
    .B3(reg_8bit_8_b3), .B2(reg_8bit_8_b2), .B1(reg_8bit_8_b1), .B0(reg_8bit_8_b0));
  assign O6 = Read ? D6 : 1'bz;  // Controlled_Buffer controlled_buffer_2
  assign O5 = Read ? D5 : 1'bz;  // Controlled_Buffer controlled_buffer_3
  assign O4 = Read ? D4 : 1'bz;  // Controlled_Buffer controlled_buffer_4
  assign O3 = Read ? D3 : 1'bz;  // Controlled_Buffer controlled_buffer_5
  and and_1 (and_1_out, address_decoder_4_bits_1_df, Write);
  and and_2 (and_2_out, address_decoder_4_bits_1_de, Write);
  and and_3 (and_3_out, address_decoder_4_bits_1_dd, Write);
  and and_4 (and_4_out, address_decoder_4_bits_1_dc, Write);
  and and_5 (and_5_out, address_decoder_4_bits_1_db, Write);
  and and_6 (and_6_out, address_decoder_4_bits_1_da, Write);
  and and_7 (and_7_out, address_decoder_4_bits_1_d9, Write);
  and and_8 (and_8_out, address_decoder_4_bits_1_d8, Write);
  assign O2 = Read ? D2 : 1'bz;  // Controlled_Buffer controlled_buffer_6
  assign O1 = Read ? D1 : 1'bz;  // Controlled_Buffer controlled_buffer_7
  assign O0 = Read ? D0 : 1'bz;  // Controlled_Buffer controlled_buffer_8
  assign controlled_buffer_9_out = Write ? I7 : 1'bz;  // Controlled_Buffer controlled_buffer_9
  assign controlled_buffer_10_out = Write ? I6 : 1'bz;  // Controlled_Buffer controlled_buffer_10
  assign controlled_buffer_11_out = Write ? I5 : 1'bz;  // Controlled_Buffer controlled_buffer_11
  DotMatrix #(.dotshape("circle"), .inputtype("row"), .matrixcols(1), .matrixrows(8)) dotmatrix_9 (
    .row0(reg_8bit_9_b7), .row1(reg_8bit_9_b6), .row2(reg_8bit_9_b5), .row3(reg_8bit_9_b4),
    .row4(reg_8bit_9_b3), .row5(reg_8bit_9_b2), .row6(reg_8bit_9_b1), .row7(reg_8bit_9_b0));
  DotMatrix #(.dotshape("circle"), .inputtype("row"), .matrixcols(1), .matrixrows(8)) dotmatrix_10 (
    .row0(reg_8bit_10_b7), .row1(reg_8bit_10_b6), .row2(reg_8bit_10_b5), .row3(reg_8bit_10_b4),
    .row4(reg_8bit_10_b3), .row5(reg_8bit_10_b2), .row6(reg_8bit_10_b1), .row7(reg_8bit_10_b0));
  DotMatrix #(.dotshape("circle"), .inputtype("row"), .matrixcols(1), .matrixrows(8)) dotmatrix_11 (
    .row0(reg_8bit_11_b7), .row1(reg_8bit_11_b6), .row2(reg_8bit_11_b5), .row3(reg_8bit_11_b4),
    .row4(reg_8bit_11_b3), .row5(reg_8bit_11_b2), .row6(reg_8bit_11_b1), .row7(reg_8bit_11_b0));
  DotMatrix #(.dotshape("circle"), .inputtype("row"), .matrixcols(1), .matrixrows(8)) dotmatrix_12 (
    .row0(reg_8bit_12_b7), .row1(reg_8bit_12_b6), .row2(reg_8bit_12_b5), .row3(reg_8bit_12_b4),
    .row4(reg_8bit_12_b3), .row5(reg_8bit_12_b2), .row6(reg_8bit_12_b1), .row7(reg_8bit_12_b0));
  DotMatrix #(.dotshape("circle"), .inputtype("row"), .matrixcols(1), .matrixrows(8)) dotmatrix_13 (
    .row0(reg_8bit_13_b7), .row1(reg_8bit_13_b6), .row2(reg_8bit_13_b5), .row3(reg_8bit_13_b4),
    .row4(reg_8bit_13_b3), .row5(reg_8bit_13_b2), .row6(reg_8bit_13_b1), .row7(reg_8bit_13_b0));
  DotMatrix #(.dotshape("circle"), .inputtype("row"), .matrixcols(1), .matrixrows(8)) dotmatrix_14 (
    .row0(reg_8bit_14_b7), .row1(reg_8bit_14_b6), .row2(reg_8bit_14_b5), .row3(reg_8bit_14_b4),
    .row4(reg_8bit_14_b3), .row5(reg_8bit_14_b2), .row6(reg_8bit_14_b1), .row7(reg_8bit_14_b0));
  DotMatrix #(.dotshape("circle"), .inputtype("row"), .matrixcols(1), .matrixrows(8)) dotmatrix_15 (
    .row0(reg_8bit_15_b7), .row1(reg_8bit_15_b6), .row2(reg_8bit_15_b5), .row3(reg_8bit_15_b4),
    .row4(reg_8bit_15_b3), .row5(reg_8bit_15_b2), .row6(reg_8bit_15_b1), .row7(reg_8bit_15_b0));
  DotMatrix #(.dotshape("circle"), .inputtype("row"), .matrixcols(1), .matrixrows(8)) dotmatrix_16 (
    .row0(reg_8bit_16_b7), .row1(reg_8bit_16_b6), .row2(reg_8bit_16_b5), .row3(reg_8bit_16_b4),
    .row4(reg_8bit_16_b3), .row5(reg_8bit_16_b2), .row6(reg_8bit_16_b1), .row7(reg_8bit_16_b0));
  assign controlled_buffer_12_out = Write ? I4 : 1'bz;  // Controlled_Buffer controlled_buffer_12
  assign controlled_buffer_13_out = Write ? I3 : 1'bz;  // Controlled_Buffer controlled_buffer_13
  assign controlled_buffer_14_out = Write ? I2 : 1'bz;  // Controlled_Buffer controlled_buffer_14
  assign controlled_buffer_15_out = Write ? I1 : 1'bz;  // Controlled_Buffer controlled_buffer_15
  assign controlled_buffer_16_out = Write ? I0 : 1'bz;  // Controlled_Buffer controlled_buffer_16
  Reg_8bit reg_8bit_9 (
    .I7(controlled_buffer_9_out), .I6(controlled_buffer_10_out), .I5(controlled_buffer_11_out),
    .I4(controlled_buffer_12_out), .I3(controlled_buffer_13_out), .I2(controlled_buffer_14_out),
    .I1(controlled_buffer_15_out), .I0(controlled_buffer_16_out), .Clock(Clock), .Load(and_9_out),
    .RST(Clear), .En(address_decoder_4_bits_1_d0), .O7(D7), .O6(D6), .O5(D5), .O4(D4), .O3(D3), .O2(D2),
    .O1(D1), .O0(D0), .B7(reg_8bit_9_b7), .B6(reg_8bit_9_b6), .B5(reg_8bit_9_b5), .B4(reg_8bit_9_b4),
    .B3(reg_8bit_9_b3), .B2(reg_8bit_9_b2), .B1(reg_8bit_9_b1), .B0(reg_8bit_9_b0));
  Reg_8bit reg_8bit_10 (
    .I7(controlled_buffer_9_out), .I6(controlled_buffer_10_out), .I5(controlled_buffer_11_out),
    .I4(controlled_buffer_12_out), .I3(controlled_buffer_13_out), .I2(controlled_buffer_14_out),
    .I1(controlled_buffer_15_out), .I0(controlled_buffer_16_out), .Clock(Clock), .Load(and_10_out),
    .RST(Clear), .En(address_decoder_4_bits_1_d1), .O7(D7), .O6(D6), .O5(D5), .O4(D4), .O3(D3), .O2(D2),
    .O1(D1), .O0(D0), .B7(reg_8bit_10_b7), .B6(reg_8bit_10_b6), .B5(reg_8bit_10_b5), .B4(reg_8bit_10_b4),
    .B3(reg_8bit_10_b3), .B2(reg_8bit_10_b2), .B1(reg_8bit_10_b1), .B0(reg_8bit_10_b0));
  Reg_8bit reg_8bit_11 (
    .I7(controlled_buffer_9_out), .I6(controlled_buffer_10_out), .I5(controlled_buffer_11_out),
    .I4(controlled_buffer_12_out), .I3(controlled_buffer_13_out), .I2(controlled_buffer_14_out),
    .I1(controlled_buffer_15_out), .I0(controlled_buffer_16_out), .Clock(Clock), .Load(and_11_out),
    .RST(Clear), .En(address_decoder_4_bits_1_d2), .O7(D7), .O6(D6), .O5(D5), .O4(D4), .O3(D3), .O2(D2),
    .O1(D1), .O0(D0), .B7(reg_8bit_11_b7), .B6(reg_8bit_11_b6), .B5(reg_8bit_11_b5), .B4(reg_8bit_11_b4),
    .B3(reg_8bit_11_b3), .B2(reg_8bit_11_b2), .B1(reg_8bit_11_b1), .B0(reg_8bit_11_b0));
  Reg_8bit reg_8bit_12 (
    .I7(controlled_buffer_9_out), .I6(controlled_buffer_10_out), .I5(controlled_buffer_11_out),
    .I4(controlled_buffer_12_out), .I3(controlled_buffer_13_out), .I2(controlled_buffer_14_out),
    .I1(controlled_buffer_15_out), .I0(controlled_buffer_16_out), .Clock(Clock), .Load(and_12_out),
    .RST(Clear), .En(address_decoder_4_bits_1_d3), .O7(D7), .O6(D6), .O5(D5), .O4(D4), .O3(D3), .O2(D2),
    .O1(D1), .O0(D0), .B7(reg_8bit_12_b7), .B6(reg_8bit_12_b6), .B5(reg_8bit_12_b5), .B4(reg_8bit_12_b4),
    .B3(reg_8bit_12_b3), .B2(reg_8bit_12_b2), .B1(reg_8bit_12_b1), .B0(reg_8bit_12_b0));
  Reg_8bit reg_8bit_13 (
    .I7(controlled_buffer_9_out), .I6(controlled_buffer_10_out), .I5(controlled_buffer_11_out),
    .I4(controlled_buffer_12_out), .I3(controlled_buffer_13_out), .I2(controlled_buffer_14_out),
    .I1(controlled_buffer_15_out), .I0(controlled_buffer_16_out), .Clock(Clock), .Load(and_13_out),
    .RST(Clear), .En(address_decoder_4_bits_1_d4), .O7(D7), .O6(D6), .O5(D5), .O4(D4), .O3(D3), .O2(D2),
    .O1(D1), .O0(D0), .B7(reg_8bit_13_b7), .B6(reg_8bit_13_b6), .B5(reg_8bit_13_b5), .B4(reg_8bit_13_b4),
    .B3(reg_8bit_13_b3), .B2(reg_8bit_13_b2), .B1(reg_8bit_13_b1), .B0(reg_8bit_13_b0));
  Reg_8bit reg_8bit_14 (
    .I7(controlled_buffer_9_out), .I6(controlled_buffer_10_out), .I5(controlled_buffer_11_out),
    .I4(controlled_buffer_12_out), .I3(controlled_buffer_13_out), .I2(controlled_buffer_14_out),
    .I1(controlled_buffer_15_out), .I0(controlled_buffer_16_out), .Clock(Clock), .Load(and_14_out),
    .RST(Clear), .En(address_decoder_4_bits_1_d5), .O7(D7), .O6(D6), .O5(D5), .O4(D4), .O3(D3), .O2(D2),
    .O1(D1), .O0(D0), .B7(reg_8bit_14_b7), .B6(reg_8bit_14_b6), .B5(reg_8bit_14_b5), .B4(reg_8bit_14_b4),
    .B3(reg_8bit_14_b3), .B2(reg_8bit_14_b2), .B1(reg_8bit_14_b1), .B0(reg_8bit_14_b0));
  Reg_8bit reg_8bit_15 (
    .I7(controlled_buffer_9_out), .I6(controlled_buffer_10_out), .I5(controlled_buffer_11_out),
    .I4(controlled_buffer_12_out), .I3(controlled_buffer_13_out), .I2(controlled_buffer_14_out),
    .I1(controlled_buffer_15_out), .I0(controlled_buffer_16_out), .Clock(Clock), .Load(and_15_out),
    .RST(Clear), .En(address_decoder_4_bits_1_d6), .O7(D7), .O6(D6), .O5(D5), .O4(D4), .O3(D3), .O2(D2),
    .O1(D1), .O0(D0), .B7(reg_8bit_15_b7), .B6(reg_8bit_15_b6), .B5(reg_8bit_15_b5), .B4(reg_8bit_15_b4),
    .B3(reg_8bit_15_b3), .B2(reg_8bit_15_b2), .B1(reg_8bit_15_b1), .B0(reg_8bit_15_b0));
  Reg_8bit reg_8bit_16 (
    .I7(controlled_buffer_9_out), .I6(controlled_buffer_10_out), .I5(controlled_buffer_11_out),
    .I4(controlled_buffer_12_out), .I3(controlled_buffer_13_out), .I2(controlled_buffer_14_out),
    .I1(controlled_buffer_15_out), .I0(controlled_buffer_16_out), .Clock(Clock), .Load(and_16_out),
    .RST(Clear), .En(address_decoder_4_bits_1_d7), .O7(D7), .O6(D6), .O5(D5), .O4(D4), .O3(D3), .O2(D2),
    .O1(D1), .O0(D0), .B7(reg_8bit_16_b7), .B6(reg_8bit_16_b6), .B5(reg_8bit_16_b5), .B4(reg_8bit_16_b4),
    .B3(reg_8bit_16_b3), .B2(reg_8bit_16_b2), .B1(reg_8bit_16_b1), .B0(reg_8bit_16_b0));
  and and_9 (and_9_out, Write, address_decoder_4_bits_1_d0);
  and and_10 (and_10_out, Write, address_decoder_4_bits_1_d1);
  and and_11 (and_11_out, Write, address_decoder_4_bits_1_d2);
  and and_12 (and_12_out, Write, address_decoder_4_bits_1_d3);
  and and_13 (and_13_out, Write, address_decoder_4_bits_1_d4);
  and and_14 (and_14_out, Write, address_decoder_4_bits_1_d5);
  and and_15 (and_15_out, Write, address_decoder_4_bits_1_d6);
  and and_16 (and_16_out, Write, address_decoder_4_bits_1_d7);
endmodule

// RAM
module SRAM_256_bytes (
  input  I7,
  input  I6,
  input  I5,
  input  I4,
  input  I3,
  input  I2,
  input  I1,
  input  I0,
  input  Read,
  input  Write,
  input  Clear,
  input  Clock,
  input  A7,
  input  A6,
  input  A5,
  input  A4,
  input  A3,
  input  A2,
  input  A1,
  input  A0,
  output S7,
  output S6,
  output S5,
  output S4,
  output S3,
  output S2,
  output S1,
  output S0,
  output O7,
  output O6,
  output O5,
  output O4,
  output O3,
  output O2,
  output O1,
  output O0
);

  wire address_decoder_4_bits_1_d0, address_decoder_4_bits_1_d1, address_decoder_4_bits_1_d2,
       address_decoder_4_bits_1_d3, address_decoder_4_bits_1_d4, address_decoder_4_bits_1_d5,
       address_decoder_4_bits_1_d6, address_decoder_4_bits_1_d7, address_decoder_4_bits_1_d8,
       address_decoder_4_bits_1_d9, address_decoder_4_bits_1_da, address_decoder_4_bits_1_db,
       address_decoder_4_bits_1_dc, address_decoder_4_bits_1_dd, address_decoder_4_bits_1_de,
       address_decoder_4_bits_1_df, and_1_out, and_2_out, and_3_out, and_4_out, and_5_out, and_6_out,
       and_7_out, and_8_out, and_9_out, and_10_out, and_11_out, and_12_out, and_13_out, and_14_out,
       and_15_out, and_16_out, controlled_buffer_9_out, controlled_buffer_10_out, controlled_buffer_11_out,
       controlled_buffer_12_out, controlled_buffer_13_out, controlled_buffer_14_out,
       controlled_buffer_15_out, controlled_buffer_16_out, sram_16_bytes_1_d0, sram_16_bytes_1_d1,
       sram_16_bytes_1_d2, sram_16_bytes_1_d3, sram_16_bytes_1_d4, sram_16_bytes_1_d5, sram_16_bytes_1_d6,
       sram_16_bytes_1_d7, sram_16_bytes_2_d0, sram_16_bytes_2_d1, sram_16_bytes_2_d2, sram_16_bytes_2_d3,
       sram_16_bytes_2_d4, sram_16_bytes_2_d5, sram_16_bytes_2_d6, sram_16_bytes_2_d7, sram_16_bytes_3_d0,
       sram_16_bytes_3_d1, sram_16_bytes_3_d2, sram_16_bytes_3_d3, sram_16_bytes_3_d4, sram_16_bytes_3_d5,
       sram_16_bytes_3_d6, sram_16_bytes_3_d7, sram_16_bytes_4_d0, sram_16_bytes_4_d1, sram_16_bytes_4_d2,
       sram_16_bytes_4_d3, sram_16_bytes_4_d4, sram_16_bytes_4_d5, sram_16_bytes_4_d6, sram_16_bytes_4_d7,
       sram_16_bytes_5_d0, sram_16_bytes_5_d1, sram_16_bytes_5_d2, sram_16_bytes_5_d3, sram_16_bytes_5_d4,
       sram_16_bytes_5_d5, sram_16_bytes_5_d6, sram_16_bytes_5_d7, sram_16_bytes_6_d0, sram_16_bytes_6_d1,
       sram_16_bytes_6_d2, sram_16_bytes_6_d3, sram_16_bytes_6_d4, sram_16_bytes_6_d5, sram_16_bytes_6_d6,
       sram_16_bytes_6_d7, sram_16_bytes_7_d0, sram_16_bytes_7_d1, sram_16_bytes_7_d2, sram_16_bytes_7_d3,
       sram_16_bytes_7_d4, sram_16_bytes_7_d5, sram_16_bytes_7_d6, sram_16_bytes_7_d7, sram_16_bytes_8_d0,
       sram_16_bytes_8_d1, sram_16_bytes_8_d2, sram_16_bytes_8_d3, sram_16_bytes_8_d4, sram_16_bytes_8_d5,
       sram_16_bytes_8_d6, sram_16_bytes_8_d7, sram_16_bytes_9_d0, sram_16_bytes_9_d1, sram_16_bytes_9_d2,
       sram_16_bytes_9_d3, sram_16_bytes_9_d4, sram_16_bytes_9_d5, sram_16_bytes_9_d6, sram_16_bytes_9_d7,
       sram_16_bytes_10_d0, sram_16_bytes_10_d1, sram_16_bytes_10_d2, sram_16_bytes_10_d3,
       sram_16_bytes_10_d4, sram_16_bytes_10_d5, sram_16_bytes_10_d6, sram_16_bytes_10_d7,
       sram_16_bytes_11_d0, sram_16_bytes_11_d1, sram_16_bytes_11_d2, sram_16_bytes_11_d3,
       sram_16_bytes_11_d4, sram_16_bytes_11_d5, sram_16_bytes_11_d6, sram_16_bytes_11_d7,
       sram_16_bytes_12_d0, sram_16_bytes_12_d1, sram_16_bytes_12_d2, sram_16_bytes_12_d3,
       sram_16_bytes_12_d4, sram_16_bytes_12_d5, sram_16_bytes_12_d6, sram_16_bytes_12_d7,
       sram_16_bytes_13_d0, sram_16_bytes_13_d1, sram_16_bytes_13_d2, sram_16_bytes_13_d3,
       sram_16_bytes_13_d4, sram_16_bytes_13_d5, sram_16_bytes_13_d6, sram_16_bytes_13_d7,
       sram_16_bytes_14_d0, sram_16_bytes_14_d1, sram_16_bytes_14_d2, sram_16_bytes_14_d3,
       sram_16_bytes_14_d4, sram_16_bytes_14_d5, sram_16_bytes_14_d6, sram_16_bytes_14_d7,
       sram_16_bytes_15_d0, sram_16_bytes_15_d1, sram_16_bytes_15_d2, sram_16_bytes_15_d3,
       sram_16_bytes_15_d4, sram_16_bytes_15_d5, sram_16_bytes_15_d6, sram_16_bytes_15_d7,
       sram_16_bytes_16_d0, sram_16_bytes_16_d1, sram_16_bytes_16_d2, sram_16_bytes_16_d3,
       sram_16_bytes_16_d4, sram_16_bytes_16_d5, sram_16_bytes_16_d6, sram_16_bytes_16_d7;

  Address_Decoder_4_bits address_decoder_4_bits_1 (
    .Enable(1'b1), .A1(A5), .A0(A4), .A3(A7), .A2(A6), .DF(address_decoder_4_bits_1_df),
    .DE(address_decoder_4_bits_1_de), .DD(address_decoder_4_bits_1_dd), .DC(address_decoder_4_bits_1_dc),
    .DB(address_decoder_4_bits_1_db), .DA(address_decoder_4_bits_1_da), .D9(address_decoder_4_bits_1_d9),
    .D8(address_decoder_4_bits_1_d8), .D7(address_decoder_4_bits_1_d7), .D6(address_decoder_4_bits_1_d6),
    .D5(address_decoder_4_bits_1_d5), .D4(address_decoder_4_bits_1_d4), .D3(address_decoder_4_bits_1_d3),
    .D2(address_decoder_4_bits_1_d2), .D1(address_decoder_4_bits_1_d1), .D0(address_decoder_4_bits_1_d0));
  and and_1 (and_1_out, address_decoder_4_bits_1_d7, Write);
  and and_2 (and_2_out, address_decoder_4_bits_1_d6, Write);
  and and_3 (and_3_out, address_decoder_4_bits_1_d5, Write);
  and and_4 (and_4_out, address_decoder_4_bits_1_d4, Write);
  and and_5 (and_5_out, address_decoder_4_bits_1_d3, Write);
  and and_6 (and_6_out, address_decoder_4_bits_1_d2, Write);
  and and_7 (and_7_out, address_decoder_4_bits_1_d1, Write);
  and and_8 (and_8_out, address_decoder_4_bits_1_d0, Write);
  assign O7 = Read ? S7 : 1'bz;  // Controlled_Buffer controlled_buffer_1
  assign O6 = Read ? S6 : 1'bz;  // Controlled_Buffer controlled_buffer_2
  assign O5 = Read ? S5 : 1'bz;  // Controlled_Buffer controlled_buffer_3
  assign O4 = Read ? S4 : 1'bz;  // Controlled_Buffer controlled_buffer_4
  assign O3 = Read ? S3 : 1'bz;  // Controlled_Buffer controlled_buffer_5
  DotMatrix #(.dotshape("circle"), .inputtype("row"), .matrixcols(1), .matrixrows(8)) dotmatrix_1 (
    .row0(sram_16_bytes_1_d7), .row1(sram_16_bytes_1_d6), .row2(sram_16_bytes_1_d5),
    .row3(sram_16_bytes_1_d4), .row4(sram_16_bytes_1_d3), .row5(sram_16_bytes_1_d2),
    .row6(sram_16_bytes_1_d1), .row7(sram_16_bytes_1_d0));
  SRAM_16_bytes sram_16_bytes_1 (
    .Read(address_decoder_4_bits_1_d7), .Write(and_1_out), .Clear(Clear), .Clock(Clock), .A3(A3), .A2(A2),
    .A1(A1), .A0(A0), .I7(controlled_buffer_9_out), .I6(controlled_buffer_10_out),
    .I5(controlled_buffer_11_out), .I4(controlled_buffer_12_out), .I3(controlled_buffer_13_out),
    .I2(controlled_buffer_14_out), .I1(controlled_buffer_15_out), .I0(controlled_buffer_16_out),
    .D7(sram_16_bytes_1_d7), .D6(sram_16_bytes_1_d6), .D5(sram_16_bytes_1_d5), .D4(sram_16_bytes_1_d4),
    .D3(sram_16_bytes_1_d3), .D2(sram_16_bytes_1_d2), .D1(sram_16_bytes_1_d1), .D0(sram_16_bytes_1_d0),
    .O7(S7), .O6(S6), .O5(S5), .O4(S4), .O3(S3), .O2(S2), .O1(S1), .O0(S0));
  DotMatrix #(.dotshape("circle"), .inputtype("row"), .matrixcols(1), .matrixrows(8)) dotmatrix_2 (
    .row0(sram_16_bytes_2_d7), .row1(sram_16_bytes_2_d6), .row2(sram_16_bytes_2_d5),
    .row3(sram_16_bytes_2_d4), .row4(sram_16_bytes_2_d3), .row5(sram_16_bytes_2_d2),
    .row6(sram_16_bytes_2_d1), .row7(sram_16_bytes_2_d0));
  SRAM_16_bytes sram_16_bytes_2 (
    .Read(address_decoder_4_bits_1_d6), .Write(and_2_out), .Clear(Clear), .Clock(Clock), .A3(A3), .A2(A2),
    .A1(A1), .A0(A0), .I7(controlled_buffer_9_out), .I6(controlled_buffer_10_out),
    .I5(controlled_buffer_11_out), .I4(controlled_buffer_12_out), .I3(controlled_buffer_13_out),
    .I2(controlled_buffer_14_out), .I1(controlled_buffer_15_out), .I0(controlled_buffer_16_out),
    .D7(sram_16_bytes_2_d7), .D6(sram_16_bytes_2_d6), .D5(sram_16_bytes_2_d5), .D4(sram_16_bytes_2_d4),
    .D3(sram_16_bytes_2_d3), .D2(sram_16_bytes_2_d2), .D1(sram_16_bytes_2_d1), .D0(sram_16_bytes_2_d0),
    .O7(S7), .O6(S6), .O5(S5), .O4(S4), .O3(S3), .O2(S2), .O1(S1), .O0(S0));
  DotMatrix #(.dotshape("circle"), .inputtype("row"), .matrixcols(1), .matrixrows(8)) dotmatrix_3 (
    .row0(sram_16_bytes_3_d7), .row1(sram_16_bytes_3_d6), .row2(sram_16_bytes_3_d5),
    .row3(sram_16_bytes_3_d4), .row4(sram_16_bytes_3_d3), .row5(sram_16_bytes_3_d2),
    .row6(sram_16_bytes_3_d1), .row7(sram_16_bytes_3_d0));
  SRAM_16_bytes sram_16_bytes_3 (
    .Read(address_decoder_4_bits_1_d5), .Write(and_3_out), .Clear(Clear), .Clock(Clock), .A3(A3), .A2(A2),
    .A1(A1), .A0(A0), .I7(controlled_buffer_9_out), .I6(controlled_buffer_10_out),
    .I5(controlled_buffer_11_out), .I4(controlled_buffer_12_out), .I3(controlled_buffer_13_out),
    .I2(controlled_buffer_14_out), .I1(controlled_buffer_15_out), .I0(controlled_buffer_16_out),
    .D7(sram_16_bytes_3_d7), .D6(sram_16_bytes_3_d6), .D5(sram_16_bytes_3_d5), .D4(sram_16_bytes_3_d4),
    .D3(sram_16_bytes_3_d3), .D2(sram_16_bytes_3_d2), .D1(sram_16_bytes_3_d1), .D0(sram_16_bytes_3_d0),
    .O7(S7), .O6(S6), .O5(S5), .O4(S4), .O3(S3), .O2(S2), .O1(S1), .O0(S0));
  DotMatrix #(.dotshape("circle"), .inputtype("row"), .matrixcols(1), .matrixrows(8)) dotmatrix_4 (
    .row0(sram_16_bytes_4_d7), .row1(sram_16_bytes_4_d6), .row2(sram_16_bytes_4_d5),
    .row3(sram_16_bytes_4_d4), .row4(sram_16_bytes_4_d3), .row5(sram_16_bytes_4_d2),
    .row6(sram_16_bytes_4_d1), .row7(sram_16_bytes_4_d0));
  SRAM_16_bytes sram_16_bytes_4 (
    .Read(address_decoder_4_bits_1_d4), .Write(and_4_out), .Clear(Clear), .Clock(Clock), .A3(A3), .A2(A2),
    .A1(A1), .A0(A0), .I7(controlled_buffer_9_out), .I6(controlled_buffer_10_out),
    .I5(controlled_buffer_11_out), .I4(controlled_buffer_12_out), .I3(controlled_buffer_13_out),
    .I2(controlled_buffer_14_out), .I1(controlled_buffer_15_out), .I0(controlled_buffer_16_out),
    .D7(sram_16_bytes_4_d7), .D6(sram_16_bytes_4_d6), .D5(sram_16_bytes_4_d5), .D4(sram_16_bytes_4_d4),
    .D3(sram_16_bytes_4_d3), .D2(sram_16_bytes_4_d2), .D1(sram_16_bytes_4_d1), .D0(sram_16_bytes_4_d0),
    .O7(S7), .O6(S6), .O5(S5), .O4(S4), .O3(S3), .O2(S2), .O1(S1), .O0(S0));
  DotMatrix #(.dotshape("circle"), .inputtype("row"), .matrixcols(1), .matrixrows(8)) dotmatrix_5 (
    .row0(sram_16_bytes_5_d7), .row1(sram_16_bytes_5_d6), .row2(sram_16_bytes_5_d5),
    .row3(sram_16_bytes_5_d4), .row4(sram_16_bytes_5_d3), .row5(sram_16_bytes_5_d2),
    .row6(sram_16_bytes_5_d1), .row7(sram_16_bytes_5_d0));
  SRAM_16_bytes sram_16_bytes_5 (
    .Read(address_decoder_4_bits_1_d3), .Write(and_5_out), .Clear(Clear), .Clock(Clock), .A3(A3), .A2(A2),
    .A1(A1), .A0(A0), .I7(controlled_buffer_9_out), .I6(controlled_buffer_10_out),
    .I5(controlled_buffer_11_out), .I4(controlled_buffer_12_out), .I3(controlled_buffer_13_out),
    .I2(controlled_buffer_14_out), .I1(controlled_buffer_15_out), .I0(controlled_buffer_16_out),
    .D7(sram_16_bytes_5_d7), .D6(sram_16_bytes_5_d6), .D5(sram_16_bytes_5_d5), .D4(sram_16_bytes_5_d4),
    .D3(sram_16_bytes_5_d3), .D2(sram_16_bytes_5_d2), .D1(sram_16_bytes_5_d1), .D0(sram_16_bytes_5_d0),
    .O7(S7), .O6(S6), .O5(S5), .O4(S4), .O3(S3), .O2(S2), .O1(S1), .O0(S0));
  DotMatrix #(.dotshape("circle"), .inputtype("row"), .matrixcols(1), .matrixrows(8)) dotmatrix_6 (
    .row0(sram_16_bytes_6_d7), .row1(sram_16_bytes_6_d6), .row2(sram_16_bytes_6_d5),
    .row3(sram_16_bytes_6_d4), .row4(sram_16_bytes_6_d3), .row5(sram_16_bytes_6_d2),
    .row6(sram_16_bytes_6_d1), .row7(sram_16_bytes_6_d0));
  SRAM_16_bytes sram_16_bytes_6 (
    .Read(address_decoder_4_bits_1_d2), .Write(and_6_out), .Clear(Clear), .Clock(Clock), .A3(A3), .A2(A2),
    .A1(A1), .A0(A0), .I7(controlled_buffer_9_out), .I6(controlled_buffer_10_out),
    .I5(controlled_buffer_11_out), .I4(controlled_buffer_12_out), .I3(controlled_buffer_13_out),
    .I2(controlled_buffer_14_out), .I1(controlled_buffer_15_out), .I0(controlled_buffer_16_out),
    .D7(sram_16_bytes_6_d7), .D6(sram_16_bytes_6_d6), .D5(sram_16_bytes_6_d5), .D4(sram_16_bytes_6_d4),
    .D3(sram_16_bytes_6_d3), .D2(sram_16_bytes_6_d2), .D1(sram_16_bytes_6_d1), .D0(sram_16_bytes_6_d0),
    .O7(S7), .O6(S6), .O5(S5), .O4(S4), .O3(S3), .O2(S2), .O1(S1), .O0(S0));
  DotMatrix #(.dotshape("circle"), .inputtype("row"), .matrixcols(1), .matrixrows(8)) dotmatrix_7 (
    .row0(sram_16_bytes_7_d7), .row1(sram_16_bytes_7_d6), .row2(sram_16_bytes_7_d5),
    .row3(sram_16_bytes_7_d4), .row4(sram_16_bytes_7_d3), .row5(sram_16_bytes_7_d2),
    .row6(sram_16_bytes_7_d1), .row7(sram_16_bytes_7_d0));
  SRAM_16_bytes sram_16_bytes_7 (
    .Read(address_decoder_4_bits_1_d1), .Write(and_7_out), .Clear(Clear), .Clock(Clock), .A3(A3), .A2(A2),
    .A1(A1), .A0(A0), .I7(controlled_buffer_9_out), .I6(controlled_buffer_10_out),
    .I5(controlled_buffer_11_out), .I4(controlled_buffer_12_out), .I3(controlled_buffer_13_out),
    .I2(controlled_buffer_14_out), .I1(controlled_buffer_15_out), .I0(controlled_buffer_16_out),
    .D7(sram_16_bytes_7_d7), .D6(sram_16_bytes_7_d6), .D5(sram_16_bytes_7_d5), .D4(sram_16_bytes_7_d4),
    .D3(sram_16_bytes_7_d3), .D2(sram_16_bytes_7_d2), .D1(sram_16_bytes_7_d1), .D0(sram_16_bytes_7_d0),
    .O7(S7), .O6(S6), .O5(S5), .O4(S4), .O3(S3), .O2(S2), .O1(S1), .O0(S0));
  DotMatrix #(.dotshape("circle"), .inputtype("row"), .matrixcols(1), .matrixrows(8)) dotmatrix_8 (
    .row0(sram_16_bytes_8_d7), .row1(sram_16_bytes_8_d6), .row2(sram_16_bytes_8_d5),
    .row3(sram_16_bytes_8_d4), .row4(sram_16_bytes_8_d3), .row5(sram_16_bytes_8_d2),
    .row6(sram_16_bytes_8_d1), .row7(sram_16_bytes_8_d0));
  SRAM_16_bytes sram_16_bytes_8 (
    .Read(address_decoder_4_bits_1_d0), .Write(and_8_out), .Clear(Clear), .Clock(Clock), .A3(A3), .A2(A2),
    .A1(A1), .A0(A0), .I7(controlled_buffer_9_out), .I6(controlled_buffer_10_out),
    .I5(controlled_buffer_11_out), .I4(controlled_buffer_12_out), .I3(controlled_buffer_13_out),
    .I2(controlled_buffer_14_out), .I1(controlled_buffer_15_out), .I0(controlled_buffer_16_out),
    .D7(sram_16_bytes_8_d7), .D6(sram_16_bytes_8_d6), .D5(sram_16_bytes_8_d5), .D4(sram_16_bytes_8_d4),
    .D3(sram_16_bytes_8_d3), .D2(sram_16_bytes_8_d2), .D1(sram_16_bytes_8_d1), .D0(sram_16_bytes_8_d0),
    .O7(S7), .O6(S6), .O5(S5), .O4(S4), .O3(S3), .O2(S2), .O1(S1), .O0(S0));
  assign O2 = Read ? S2 : 1'bz;  // Controlled_Buffer controlled_buffer_6
  assign O1 = Read ? S1 : 1'bz;  // Controlled_Buffer controlled_buffer_7
  assign O0 = Read ? S0 : 1'bz;  // Controlled_Buffer controlled_buffer_8
  assign controlled_buffer_9_out = Write ? I7 : 1'bz;  // Controlled_Buffer controlled_buffer_9
  assign controlled_buffer_10_out = Write ? I6 : 1'bz;  // Controlled_Buffer controlled_buffer_10
  assign controlled_buffer_11_out = Write ? I5 : 1'bz;  // Controlled_Buffer controlled_buffer_11
  assign controlled_buffer_12_out = Write ? I4 : 1'bz;  // Controlled_Buffer controlled_buffer_12
  assign controlled_buffer_13_out = Write ? I3 : 1'bz;  // Controlled_Buffer controlled_buffer_13
  assign controlled_buffer_14_out = Write ? I2 : 1'bz;  // Controlled_Buffer controlled_buffer_14
  assign controlled_buffer_15_out = Write ? I1 : 1'bz;  // Controlled_Buffer controlled_buffer_15
  assign controlled_buffer_16_out = Write ? I0 : 1'bz;  // Controlled_Buffer controlled_buffer_16
  and and_9 (and_9_out, address_decoder_4_bits_1_df, Write);
  and and_10 (and_10_out, address_decoder_4_bits_1_de, Write);
  and and_11 (and_11_out, address_decoder_4_bits_1_dd, Write);
  and and_12 (and_12_out, address_decoder_4_bits_1_dc, Write);
  and and_13 (and_13_out, address_decoder_4_bits_1_db, Write);
  and and_14 (and_14_out, address_decoder_4_bits_1_da, Write);
  and and_15 (and_15_out, address_decoder_4_bits_1_d9, Write);
  and and_16 (and_16_out, address_decoder_4_bits_1_d8, Write);
  DotMatrix #(.dotshape("circle"), .inputtype("row"), .matrixcols(1), .matrixrows(8)) dotmatrix_9 (
    .row0(sram_16_bytes_9_d7), .row1(sram_16_bytes_9_d6), .row2(sram_16_bytes_9_d5),
    .row3(sram_16_bytes_9_d4), .row4(sram_16_bytes_9_d3), .row5(sram_16_bytes_9_d2),
    .row6(sram_16_bytes_9_d1), .row7(sram_16_bytes_9_d0));
  SRAM_16_bytes sram_16_bytes_9 (
    .Read(address_decoder_4_bits_1_df), .Write(and_9_out), .Clear(Clear), .Clock(Clock), .A3(A3), .A2(A2),
    .A1(A1), .A0(A0), .I7(controlled_buffer_9_out), .I6(controlled_buffer_10_out),
    .I5(controlled_buffer_11_out), .I4(controlled_buffer_12_out), .I3(controlled_buffer_13_out),
    .I2(controlled_buffer_14_out), .I1(controlled_buffer_15_out), .I0(controlled_buffer_16_out),
    .D7(sram_16_bytes_9_d7), .D6(sram_16_bytes_9_d6), .D5(sram_16_bytes_9_d5), .D4(sram_16_bytes_9_d4),
    .D3(sram_16_bytes_9_d3), .D2(sram_16_bytes_9_d2), .D1(sram_16_bytes_9_d1), .D0(sram_16_bytes_9_d0),
    .O7(S7), .O6(S6), .O5(S5), .O4(S4), .O3(S3), .O2(S2), .O1(S1), .O0(S0));
  DotMatrix #(.dotshape("circle"), .inputtype("row"), .matrixcols(1), .matrixrows(8)) dotmatrix_10 (
    .row0(sram_16_bytes_10_d7), .row1(sram_16_bytes_10_d6), .row2(sram_16_bytes_10_d5),
    .row3(sram_16_bytes_10_d4), .row4(sram_16_bytes_10_d3), .row5(sram_16_bytes_10_d2),
    .row6(sram_16_bytes_10_d1), .row7(sram_16_bytes_10_d0));
  SRAM_16_bytes sram_16_bytes_10 (
    .Read(address_decoder_4_bits_1_de), .Write(and_10_out), .Clear(Clear), .Clock(Clock), .A3(A3), .A2(A2),
    .A1(A1), .A0(A0), .I7(controlled_buffer_9_out), .I6(controlled_buffer_10_out),
    .I5(controlled_buffer_11_out), .I4(controlled_buffer_12_out), .I3(controlled_buffer_13_out),
    .I2(controlled_buffer_14_out), .I1(controlled_buffer_15_out), .I0(controlled_buffer_16_out),
    .D7(sram_16_bytes_10_d7), .D6(sram_16_bytes_10_d6), .D5(sram_16_bytes_10_d5), .D4(sram_16_bytes_10_d4),
    .D3(sram_16_bytes_10_d3), .D2(sram_16_bytes_10_d2), .D1(sram_16_bytes_10_d1), .D0(sram_16_bytes_10_d0),
    .O7(S7), .O6(S6), .O5(S5), .O4(S4), .O3(S3), .O2(S2), .O1(S1), .O0(S0));
  DotMatrix #(.dotshape("circle"), .inputtype("row"), .matrixcols(1), .matrixrows(8)) dotmatrix_11 (
    .row0(sram_16_bytes_11_d7), .row1(sram_16_bytes_11_d6), .row2(sram_16_bytes_11_d5),
    .row3(sram_16_bytes_11_d4), .row4(sram_16_bytes_11_d3), .row5(sram_16_bytes_11_d2),
    .row6(sram_16_bytes_11_d1), .row7(sram_16_bytes_11_d0));
  SRAM_16_bytes sram_16_bytes_11 (
    .Read(address_decoder_4_bits_1_dd), .Write(and_11_out), .Clear(Clear), .Clock(Clock), .A3(A3), .A2(A2),
    .A1(A1), .A0(A0), .I7(controlled_buffer_9_out), .I6(controlled_buffer_10_out),
    .I5(controlled_buffer_11_out), .I4(controlled_buffer_12_out), .I3(controlled_buffer_13_out),
    .I2(controlled_buffer_14_out), .I1(controlled_buffer_15_out), .I0(controlled_buffer_16_out),
    .D7(sram_16_bytes_11_d7), .D6(sram_16_bytes_11_d6), .D5(sram_16_bytes_11_d5), .D4(sram_16_bytes_11_d4),
    .D3(sram_16_bytes_11_d3), .D2(sram_16_bytes_11_d2), .D1(sram_16_bytes_11_d1), .D0(sram_16_bytes_11_d0),
    .O7(S7), .O6(S6), .O5(S5), .O4(S4), .O3(S3), .O2(S2), .O1(S1), .O0(S0));
  DotMatrix #(.dotshape("circle"), .inputtype("row"), .matrixcols(1), .matrixrows(8)) dotmatrix_12 (
    .row0(sram_16_bytes_12_d7), .row1(sram_16_bytes_12_d6), .row2(sram_16_bytes_12_d5),
    .row3(sram_16_bytes_12_d4), .row4(sram_16_bytes_12_d3), .row5(sram_16_bytes_12_d2),
    .row6(sram_16_bytes_12_d1), .row7(sram_16_bytes_12_d0));
  SRAM_16_bytes sram_16_bytes_12 (
    .Read(address_decoder_4_bits_1_dc), .Write(and_12_out), .Clear(Clear), .Clock(Clock), .A3(A3), .A2(A2),
    .A1(A1), .A0(A0), .I7(controlled_buffer_9_out), .I6(controlled_buffer_10_out),
    .I5(controlled_buffer_11_out), .I4(controlled_buffer_12_out), .I3(controlled_buffer_13_out),
    .I2(controlled_buffer_14_out), .I1(controlled_buffer_15_out), .I0(controlled_buffer_16_out),
    .D7(sram_16_bytes_12_d7), .D6(sram_16_bytes_12_d6), .D5(sram_16_bytes_12_d5), .D4(sram_16_bytes_12_d4),
    .D3(sram_16_bytes_12_d3), .D2(sram_16_bytes_12_d2), .D1(sram_16_bytes_12_d1), .D0(sram_16_bytes_12_d0),
    .O7(S7), .O6(S6), .O5(S5), .O4(S4), .O3(S3), .O2(S2), .O1(S1), .O0(S0));
  DotMatrix #(.dotshape("circle"), .inputtype("row"), .matrixcols(1), .matrixrows(8)) dotmatrix_13 (
    .row0(sram_16_bytes_13_d7), .row1(sram_16_bytes_13_d6), .row2(sram_16_bytes_13_d5),
    .row3(sram_16_bytes_13_d4), .row4(sram_16_bytes_13_d3), .row5(sram_16_bytes_13_d2),
    .row6(sram_16_bytes_13_d1), .row7(sram_16_bytes_13_d0));
  SRAM_16_bytes sram_16_bytes_13 (
    .Read(address_decoder_4_bits_1_db), .Write(and_13_out), .Clear(Clear), .Clock(Clock), .A3(A3), .A2(A2),
    .A1(A1), .A0(A0), .I7(controlled_buffer_9_out), .I6(controlled_buffer_10_out),
    .I5(controlled_buffer_11_out), .I4(controlled_buffer_12_out), .I3(controlled_buffer_13_out),
    .I2(controlled_buffer_14_out), .I1(controlled_buffer_15_out), .I0(controlled_buffer_16_out),
    .D7(sram_16_bytes_13_d7), .D6(sram_16_bytes_13_d6), .D5(sram_16_bytes_13_d5), .D4(sram_16_bytes_13_d4),
    .D3(sram_16_bytes_13_d3), .D2(sram_16_bytes_13_d2), .D1(sram_16_bytes_13_d1), .D0(sram_16_bytes_13_d0),
    .O7(S7), .O6(S6), .O5(S5), .O4(S4), .O3(S3), .O2(S2), .O1(S1), .O0(S0));
  DotMatrix #(.dotshape("circle"), .inputtype("row"), .matrixcols(1), .matrixrows(8)) dotmatrix_14 (
    .row0(sram_16_bytes_14_d7), .row1(sram_16_bytes_14_d6), .row2(sram_16_bytes_14_d5),
    .row3(sram_16_bytes_14_d4), .row4(sram_16_bytes_14_d3), .row5(sram_16_bytes_14_d2),
    .row6(sram_16_bytes_14_d1), .row7(sram_16_bytes_14_d0));
  SRAM_16_bytes sram_16_bytes_14 (
    .Read(address_decoder_4_bits_1_da), .Write(and_14_out), .Clear(Clear), .Clock(Clock), .A3(A3), .A2(A2),
    .A1(A1), .A0(A0), .I7(controlled_buffer_9_out), .I6(controlled_buffer_10_out),
    .I5(controlled_buffer_11_out), .I4(controlled_buffer_12_out), .I3(controlled_buffer_13_out),
    .I2(controlled_buffer_14_out), .I1(controlled_buffer_15_out), .I0(controlled_buffer_16_out),
    .D7(sram_16_bytes_14_d7), .D6(sram_16_bytes_14_d6), .D5(sram_16_bytes_14_d5), .D4(sram_16_bytes_14_d4),
    .D3(sram_16_bytes_14_d3), .D2(sram_16_bytes_14_d2), .D1(sram_16_bytes_14_d1), .D0(sram_16_bytes_14_d0),
    .O7(S7), .O6(S6), .O5(S5), .O4(S4), .O3(S3), .O2(S2), .O1(S1), .O0(S0));
  DotMatrix #(.dotshape("circle"), .inputtype("row"), .matrixcols(1), .matrixrows(8)) dotmatrix_15 (
    .row0(sram_16_bytes_15_d7), .row1(sram_16_bytes_15_d6), .row2(sram_16_bytes_15_d5),
    .row3(sram_16_bytes_15_d4), .row4(sram_16_bytes_15_d3), .row5(sram_16_bytes_15_d2),
    .row6(sram_16_bytes_15_d1), .row7(sram_16_bytes_15_d0));
  SRAM_16_bytes sram_16_bytes_15 (
    .Read(address_decoder_4_bits_1_d9), .Write(and_15_out), .Clear(Clear), .Clock(Clock), .A3(A3), .A2(A2),
    .A1(A1), .A0(A0), .I7(controlled_buffer_9_out), .I6(controlled_buffer_10_out),
    .I5(controlled_buffer_11_out), .I4(controlled_buffer_12_out), .I3(controlled_buffer_13_out),
    .I2(controlled_buffer_14_out), .I1(controlled_buffer_15_out), .I0(controlled_buffer_16_out),
    .D7(sram_16_bytes_15_d7), .D6(sram_16_bytes_15_d6), .D5(sram_16_bytes_15_d5), .D4(sram_16_bytes_15_d4),
    .D3(sram_16_bytes_15_d3), .D2(sram_16_bytes_15_d2), .D1(sram_16_bytes_15_d1), .D0(sram_16_bytes_15_d0),
    .O7(S7), .O6(S6), .O5(S5), .O4(S4), .O3(S3), .O2(S2), .O1(S1), .O0(S0));
  DotMatrix #(.dotshape("circle"), .inputtype("row"), .matrixcols(1), .matrixrows(8)) dotmatrix_16 (
    .row0(sram_16_bytes_16_d7), .row1(sram_16_bytes_16_d6), .row2(sram_16_bytes_16_d5),
    .row3(sram_16_bytes_16_d4), .row4(sram_16_bytes_16_d3), .row5(sram_16_bytes_16_d2),
    .row6(sram_16_bytes_16_d1), .row7(sram_16_bytes_16_d0));
  SRAM_16_bytes sram_16_bytes_16 (
    .Read(address_decoder_4_bits_1_d8), .Write(and_16_out), .Clear(Clear), .Clock(Clock), .A3(A3), .A2(A2),
    .A1(A1), .A0(A0), .I7(controlled_buffer_9_out), .I6(controlled_buffer_10_out),
    .I5(controlled_buffer_11_out), .I4(controlled_buffer_12_out), .I3(controlled_buffer_13_out),
    .I2(controlled_buffer_14_out), .I1(controlled_buffer_15_out), .I0(controlled_buffer_16_out),
    .D7(sram_16_bytes_16_d7), .D6(sram_16_bytes_16_d6), .D5(sram_16_bytes_16_d5), .D4(sram_16_bytes_16_d4),
    .D3(sram_16_bytes_16_d3), .D2(sram_16_bytes_16_d2), .D1(sram_16_bytes_16_d1), .D0(sram_16_bytes_16_d0),
    .O7(S7), .O6(S6), .O5(S5), .O4(S4), .O3(S3), .O2(S2), .O1(S1), .O0(S0));
endmodule

module Decoder_8_bits_to_7_segment (
  input  [7:0] in_1,
  output a1,
  output b1,
  output c1,
  output d1,
  output e1,
  output f1,
  output g1,
  output a2,
  output b2,
  output c2,
  output d2,
  output e2,
  output f2,
  output g2,
  output a3,
  output b3,
  output c3,
  output d3,
  output e3,
  output f3,
  output g3
);

  ROM #(.dataWidth(21)) rom_1 (
    .addr(in_1), .data({g3, f3, e3, d3, c3, b3, a3, g2, f2, e2, d2, c2, b2, a2, g1, f1, e1, d1, c1, b1, a1}));

  // Notes on the sheet:
  //   contents of rom_1 (hex, n*v repeats v):
  //   3f 6 5b 4f 66 6d 7d 7 7f 6f 33f 306 35b 34f 366 36d 37d 307 37f 36f 2dbf 2d86 2ddb 2dcf 2de6 2ded
  //   2dfd 2d87 2dff 2def 27bf 2786 27db 27cf 27e6 27ed 27fd 2787 27ff 27ef 333f 3306 335b 334f 3366 336d
  //   337d 3307 337f 336f 36bf 3686 36db 36cf 36e6 36ed 36fd 3687 36ff 36ef 3ebf 3e86 3edb 3ecf 3ee6 3eed
  //   3efd 3e87 3eff 3eef 3bf 386 3db 3cf 3e6 3ed 3fd 387 3ff 3ef 3fbf 3f86 3fdb 3fcf 3fe6 3fed 3ffd 3f87
  //   3fff 3fef 37bf 3786 37db 37cf 37e6 37ed 37fd 3787 37ff 37ef 19fbf 19f86 19fdb 19fcf 19fe6 19fed
  //   19ffd 19f87 19fff 19fef 1833f 18306 1835b 1834f 18366 1836d 1837d 18307 1837f 1836f 1adbf 1ad86
  //   1addb 1adcf 1ade6 1aded 1adfd 1ad87 1adff 1adef 1a7bf 1a786 1a7db 1a7cf 1a7e6 1a7ed 1a7fd 1a787
  //   1a7ff 1a7ef 1b33f 1b306 1b35b 1b34f 1b366 1b36d 1b37d 1b307 1b37f 1b36f 1b6bf 1b686 1b6db 1b6cf
  //   1b6e6 1b6ed 1b6fd 1b687 1b6ff 1b6ef 1bebf 1be86 1bedb 1becf 1bee6 1beed 1befd 1be87 1beff 1beef
  //   183bf 18386 183db 183cf 183e6 183ed 183fd 18387 183ff 183ef 1bfbf 1bf86 1bfdb 1bfcf 1bfe6 1bfed
  //   1bffd 1bf87 1bfff 1bfef 1b7bf 1b786 1b7db 1b7cf 1b7e6 1b7ed 1b7fd 1b787 1b7ff 1b7ef 16dfbf 16df86
  //   16dfdb 16dfcf 16dfe6 16dfed 16dffd 16df87 16dfff 16dfef 16c33f 16c306 16c35b 16c34f 16c366 16c36d
  //   16c37d 16c307 16c37f 16c36f 16edbf 16ed86 16eddb 16edcf 16ede6 16eded 16edfd 16ed87 16edff 16edef
  //   16e7bf 16e786 16e7db 16e7cf 16e7e6 16e7ed 16e7fd 16e787 16e7ff 16e7ef 16f33f 16f306 16f35b 16f34f
  //   16f366 16f36d 16f37d 16f307 16f37f 16f36f 16f6bf 16f686 16f6db 16f6cf 16f6e6 16f6ed
endmodule

// FA
module FullAdder (
  input  A,
  input  B,
  input  C,
  output E,
  output Co
);

  wire and_1_out, and_2_out, xor_1_out;

  xor xor_1 (xor_1_out, A, B);
  and and_1 (and_1_out, xor_1_out, C);
  and and_2 (and_2_out, A, B);
  xor xor_2 (E, xor_1_out, C);
  or or_1 (Co, and_1_out, and_2_out);
endmodule

module ALU_2 (
  input  A7,
  input  A6,
  input  A5,
  input  A4,
  input  A3,
  input  A2,
  input  A1,
  input  A0,
  input  SE0,
  input  SE1,
  input  SE2,
  input  B7,
  input  B6,
  input  B5,
  input  B4,
  input  B3,
  input  B2,
  input  B1,
  input  B0,
  input  ALUo,
  output E7,
  output E6,
  output E5,
  output E4,
  output E3,
  output E2,
  output E1,
  output E0,
  output ZF,
  output CF,
  output S7,
  output S6,
  output S5,
  output S4,
  output S3,
  output S2,
  output S1,
  output S0
);

  wire fulladder_1_co, fulladder_2_co, fulladder_3_co, fulladder_4_co, fulladder_5_co, fulladder_6_co,
       fulladder_7_co, xor_1_out, xor_2_out, xor_3_out, xor_4_out, xor_5_out, xor_6_out, xor_7_out, xor_8_out;
  wire [7:0] and_1_out, fulladder_1_e, not_1_out, or_1_out, xor_9_out;

  xor xor_1 (xor_1_out, SE0, B7);
  xor xor_2 (xor_2_out, SE0, B6);
  assign E7 = ALUo ? S7 : 1'bz;  // Controlled_Buffer controlled_buffer_1
  assign E6 = ALUo ? S6 : 1'bz;  // Controlled_Buffer controlled_buffer_2
  assign E5 = ALUo ? S5 : 1'bz;  // Controlled_Buffer controlled_buffer_3
  assign E4 = ALUo ? S4 : 1'bz;  // Controlled_Buffer controlled_buffer_4
  assign E3 = ALUo ? S3 : 1'bz;  // Controlled_Buffer controlled_buffer_5
  assign E2 = ALUo ? S2 : 1'bz;  // Controlled_Buffer controlled_buffer_6
  assign E1 = ALUo ? S1 : 1'bz;  // Controlled_Buffer controlled_buffer_7
  assign E0 = ALUo ? S0 : 1'bz;  // Controlled_Buffer controlled_buffer_8
  xor xor_3 (xor_3_out, SE0, B5);
  xor xor_4 (xor_4_out, SE0, B4);
  xor xor_5 (xor_5_out, SE0, B3);
  xor xor_6 (xor_6_out, SE0, B2);
  xor xor_7 (xor_7_out, SE0, B1);
  xor xor_8 (xor_8_out, SE0, B0);
  FullAdder fulladder_1 (.A(A0), .B(xor_8_out), .C(SE0), .E(fulladder_1_e[0]), .Co(fulladder_1_co));
  nor nor_1 (ZF, S7, S6, S5, S4, S3, S2, S1, S0);
  FullAdder fulladder_2 (.A(A1), .B(xor_7_out), .C(fulladder_1_co), .E(fulladder_1_e[1]), .Co(fulladder_2_co));
  FullAdder fulladder_3 (.A(A2), .B(xor_6_out), .C(fulladder_2_co), .E(fulladder_1_e[2]), .Co(fulladder_3_co));
  FullAdder fulladder_4 (.A(A3), .B(xor_5_out), .C(fulladder_3_co), .E(fulladder_1_e[3]), .Co(fulladder_4_co));
  FullAdder fulladder_5 (.A(A4), .B(xor_4_out), .C(fulladder_4_co), .E(fulladder_1_e[4]), .Co(fulladder_5_co));
  FullAdder fulladder_6 (.A(A5), .B(xor_3_out), .C(fulladder_5_co), .E(fulladder_1_e[5]), .Co(fulladder_6_co));
  assign not_1_out = ~{A7, A6, A5, A4, A3, A2, A1, A0};  // NOT_Gate not_1, 8 bits wide
  assign or_1_out = {A7, A6, A5, A4, A3, A2, A1, A0} | {B7, B6, B5, B4, B3, B2, B1, B0};  // OR_Gate or_1, 8 bits wide
  assign xor_9_out = {A7, A6, A5, A4, A3, A2, A1, A0} ^ {B7, B6, B5, B4, B3, B2, B1, B0};  // XOR_Gate xor_9, 8 bits wide
  FullAdder fulladder_7 (.A(A6), .B(xor_2_out), .C(fulladder_6_co), .E(fulladder_1_e[6]), .Co(fulladder_7_co));
  assign and_1_out = {A7, A6, A5, A4, A3, A2, A1, A0} & {B7, B6, B5, B4, B3, B2, B1, B0};  // AND_Gate and_1, 8 bits wide
  FullAdder fulladder_8 (.A(A7), .B(xor_1_out), .C(fulladder_7_co), .E(fulladder_1_e[7]), .Co(CF));
  Multiplexer #(.select(3), .width(8)) multiplexer_1 (
    .in0(fulladder_1_e), .in1(fulladder_1_e), .in2(and_1_out), .in3(or_1_out), .in4(xor_9_out),
    .in5(not_1_out), .out({S7, S6, S5, S4, S3, S2, S1, S0}), .sel({SE2, SE1, SE0}));  // open: in6, in7
endmodule

module DisplaySeg (
  input  Disp,
  input  S7,
  input  S6,
  input  S5,
  input  S4,
  input  S3,
  input  S2,
  input  S1,
  input  S0,
  output [3:0] O7_4,
  output [3:0] O3_0
);

  assign O7_4[3] = Disp ? S7 : 1'bz;  // Controlled_Buffer controlled_buffer_1
  assign O7_4[2] = Disp ? S6 : 1'bz;  // Controlled_Buffer controlled_buffer_2
  assign O7_4[1] = Disp ? S5 : 1'bz;  // Controlled_Buffer controlled_buffer_3
  assign O7_4[0] = Disp ? S4 : 1'bz;  // Controlled_Buffer controlled_buffer_4
  assign O3_0[3] = Disp ? S3 : 1'bz;  // Controlled_Buffer controlled_buffer_5
  assign O3_0[2] = Disp ? S2 : 1'bz;  // Controlled_Buffer controlled_buffer_6
  assign O3_0[1] = Disp ? S1 : 1'bz;  // Controlled_Buffer controlled_buffer_7
  assign O3_0[0] = Disp ? S0 : 1'bz;  // Controlled_Buffer controlled_buffer_8
endmodule

module CPU_Design_2 (
  input  Programming_Mode
);

  wire alu_2_1_cf, alu_2_1_s0, alu_2_1_s1, alu_2_1_s2, alu_2_1_s3, alu_2_1_s4, alu_2_1_s5, alu_2_1_s6,
       alu_2_1_s7, alu_2_1_zf, and_1_out, clock_1_out, decoder_8_bits_to_7_segment_1_a1,
       decoder_8_bits_to_7_segment_1_a2, decoder_8_bits_to_7_segment_1_a3, decoder_8_bits_to_7_segment_1_b1,
       decoder_8_bits_to_7_segment_1_b2, decoder_8_bits_to_7_segment_1_b3, decoder_8_bits_to_7_segment_1_c1,
       decoder_8_bits_to_7_segment_1_c2, decoder_8_bits_to_7_segment_1_c3, decoder_8_bits_to_7_segment_1_d1,
       decoder_8_bits_to_7_segment_1_d2, decoder_8_bits_to_7_segment_1_d3, decoder_8_bits_to_7_segment_1_e1,
       decoder_8_bits_to_7_segment_1_e2, decoder_8_bits_to_7_segment_1_e3, decoder_8_bits_to_7_segment_1_f1,
       decoder_8_bits_to_7_segment_1_f2, decoder_8_bits_to_7_segment_1_f3, decoder_8_bits_to_7_segment_1_g1,
       decoder_8_bits_to_7_segment_1_g2, decoder_8_bits_to_7_segment_1_g3, dotmatrix_10_p1, dotmatrix_10_p2,
       dotmatrix_10_p3, dotmatrix_10_p4, dotmatrix_10_p5, dotmatrix_10_p6, dotmatrix_10_p7, dotmatrix_10_p8,
       instruction_decoder_1_alu_out, instruction_decoder_1_alu_s0, instruction_decoder_1_alu_s1,
       instruction_decoder_1_alu_s2, instruction_decoder_1_c_en, instruction_decoder_1_c_out,
       instruction_decoder_1_disp, instruction_decoder_1_flags_in, instruction_decoder_1_halt,
       instruction_decoder_1_ir_in, instruction_decoder_1_ir_res, instruction_decoder_1_jp,
       instruction_decoder_1_mar_in, instruction_decoder_1_ra_in, instruction_decoder_1_ra_out,
       instruction_decoder_1_rb_in, instruction_decoder_1_rb_out, instruction_decoder_1_rc_in,
       instruction_decoder_1_rc_out, instruction_decoder_1_rd_in, instruction_decoder_1_rd_out,
       instruction_decoder_1_rr, instruction_decoder_1_rw, instruction_decoder_1_s0,
       instruction_decoder_1_s1, instruction_decoder_1_s2, instruction_decoder_1_s3,
       instruction_decoder_1_s4, instruction_decoder_1_s5, instruction_decoder_1_s6,
       instruction_decoder_1_s7, or_1_out, or_2_out, program_loader_1_addr_write,
       program_loader_1_programming, program_loader_1_ram_write, reg_2bit_1_b0, reg_2bit_1_b1, reg_2bit_1_o0,
       reg_2bit_1_o1, reg_8bit_2_b0, reg_8bit_2_b1, reg_8bit_2_b2, reg_8bit_2_b3, reg_8bit_2_b4,
       reg_8bit_2_b5, reg_8bit_2_b6, reg_8bit_2_b7, reg_8bit_2_o0, reg_8bit_2_o1, reg_8bit_2_o2,
       reg_8bit_2_o3, reg_8bit_2_o4, reg_8bit_2_o5, reg_8bit_2_o6, reg_8bit_2_o7, reg_8bit_3_b0,
       reg_8bit_3_b1, reg_8bit_3_b2, reg_8bit_3_b3, reg_8bit_3_b4, reg_8bit_3_b5, reg_8bit_3_b6,
       reg_8bit_3_b7, reg_8bit_4_b0, reg_8bit_4_b1, reg_8bit_4_b2, reg_8bit_4_b3, reg_8bit_4_b4,
       reg_8bit_4_b5, reg_8bit_4_b6, reg_8bit_4_b7, reg_8bit_4_o0, reg_8bit_4_o1, reg_8bit_4_o2,
       reg_8bit_4_o3, reg_8bit_4_o4, reg_8bit_4_o5, reg_8bit_5_b0, reg_8bit_5_b1, reg_8bit_5_b2,
       reg_8bit_5_b3, reg_8bit_5_b4, reg_8bit_5_b5, reg_8bit_5_b6, reg_8bit_5_b7, reg_8bit_6_b0,
       reg_8bit_6_b1, reg_8bit_6_b2, reg_8bit_6_b3, reg_8bit_6_b4, reg_8bit_6_b5, reg_8bit_6_b6,
       reg_8bit_6_b7, reg_8bit_7_o0, reg_8bit_7_o1, reg_8bit_7_o2, reg_8bit_7_o3, reg_8bit_7_o4,
       reg_8bit_7_o5, reg_8bit_7_o6, reg_8bit_7_o7, RESET_out, reverser_1_s0, reverser_1_s1, reverser_1_s2,
       reverser_1_s3, reverser_1_s4, reverser_1_s5, reverser_1_s6, reverser_1_s7, reverser_2_s0,
       reverser_2_s1, reverser_2_s2, reverser_2_s3, reverser_2_s4, reverser_2_s5, reverser_2_s6,
       reverser_2_s7, reverser_3_s0, reverser_3_s1, reverser_3_s2, reverser_3_s3, reverser_3_s4,
       reverser_3_s5, reverser_3_s6, reverser_3_s7, RST_RAM_out;
  wire [3:0] reg_8bit_1_b3, reg_8bit_1_b7, reg_8bit_7_b0, reg_8bit_7_b4, sram_256_bytes_1_s0,
       sram_256_bytes_1_s4;
  wire [7:0] program_loader_1_rom_addr, rom_1_data;

  Hex_Digit_Display hex_digit_display_1 (.value(reg_8bit_1_b3));  // open: dp
  DotMatrix #(.dotshape("circle"), .matrixcols(8), .matrixrows(1)) dotmatrix_1 (
    .col0(reg_8bit_1_b3[3]), .col1(reg_8bit_1_b3[2]), .col2(reg_8bit_1_b3[1]), .col3(reg_8bit_1_b3[0]),
    .col4(reg_8bit_1_b7[3]), .col5(reg_8bit_1_b7[2]), .col6(reg_8bit_1_b7[1]), .col7(reg_8bit_1_b7[0]));
  Reg_8bit reg_8bit_1 (
    .I7(reg_8bit_2_o0), .I6(reg_8bit_2_o1), .I5(reg_8bit_2_o2), .I4(reg_8bit_2_o3), .I3(reg_8bit_2_o4),
    .I2(reg_8bit_2_o5), .I1(reg_8bit_2_o6), .I0(reg_8bit_2_o7), .Clock(and_1_out),
    .Load(instruction_decoder_1_disp), .RST(RESET_out), .En(1'b1), .B7(reg_8bit_1_b7[0]),
    .B6(reg_8bit_1_b7[1]), .B5(reg_8bit_1_b7[2]), .B4(reg_8bit_1_b7[3]), .B3(reg_8bit_1_b3[0]),
    .B2(reg_8bit_1_b3[1]), .B1(reg_8bit_1_b3[2]), .B0(reg_8bit_1_b3[3]));  // open: O7, O6, O5, O4, O3, O2, O1, O0
  Hex_Digit_Display hex_digit_display_2 (.value(reg_8bit_1_b7));  // open: dp
  DotMatrix #(.dotshape("circle"), .matrixcols(8), .matrixrows(1)) dotmatrix_2 (
    .col0(instruction_decoder_1_s7), .col1(instruction_decoder_1_s6), .col2(instruction_decoder_1_s5),
    .col3(instruction_decoder_1_s4), .col4(instruction_decoder_1_s3), .col5(instruction_decoder_1_s2),
    .col6(instruction_decoder_1_s1), .col7(instruction_decoder_1_s0));
  DotMatrix #(.dotshape("circle"), .matrixcols(8), .matrixrows(1)) dotmatrix_3 (
    .col0(reverser_1_s0), .col1(reverser_1_s1), .col2(reverser_1_s2), .col3(reverser_1_s3),
    .col4(reverser_1_s4), .col5(reverser_1_s5), .col6(reverser_1_s6), .col7(reverser_1_s7));
  Reg_8bit reg_8bit_2 (
    .I7(reg_8bit_2_o7), .I6(reg_8bit_2_o6), .I5(reg_8bit_2_o5), .I4(reg_8bit_2_o4), .I3(reg_8bit_2_o3),
    .I2(reg_8bit_2_o2), .I1(reg_8bit_2_o1), .I0(reg_8bit_2_o0), .Clock(and_1_out),
    .Load(instruction_decoder_1_rd_in), .RST(RESET_out), .En(instruction_decoder_1_rd_out),
    .O7(reg_8bit_2_o7), .O6(reg_8bit_2_o6), .O5(reg_8bit_2_o5), .O4(reg_8bit_2_o4), .O3(reg_8bit_2_o3),
    .O2(reg_8bit_2_o2), .O1(reg_8bit_2_o1), .O0(reg_8bit_2_o0), .B7(reg_8bit_2_b7), .B6(reg_8bit_2_b6),
    .B5(reg_8bit_2_b5), .B4(reg_8bit_2_b4), .B3(reg_8bit_2_b3), .B2(reg_8bit_2_b2), .B1(reg_8bit_2_b1),
    .B0(reg_8bit_2_b0));
  DotMatrix #(.dotshape("circle"), .matrixcols(8), .matrixrows(1)) dotmatrix_4 (
    .col0(reg_8bit_3_b7), .col1(reg_8bit_3_b6), .col2(reg_8bit_3_b5), .col3(reg_8bit_3_b4),
    .col4(reg_8bit_3_b3), .col5(reg_8bit_3_b2), .col6(reg_8bit_3_b1), .col7(reg_8bit_3_b0));
  Reverser reverser_1 (
    .E0(reg_8bit_2_b0), .E1(reg_8bit_2_b1), .E2(reg_8bit_2_b2), .E3(reg_8bit_2_b3), .E4(reg_8bit_2_b4),
    .E5(reg_8bit_2_b5), .E6(reg_8bit_2_b6), .E7(reg_8bit_2_b7), .S7(reverser_1_s7), .S6(reverser_1_s6),
    .S5(reverser_1_s5), .S4(reverser_1_s4), .S3(reverser_1_s3), .S2(reverser_1_s2), .S1(reverser_1_s1),
    .S0(reverser_1_s0));
  Reg_8bit reg_8bit_3 (
    .I7(reg_8bit_2_o7), .I6(reg_8bit_2_o6), .I5(reg_8bit_2_o5), .I4(reg_8bit_2_o4), .I3(reg_8bit_2_o3),
    .I2(reg_8bit_2_o2), .I1(reg_8bit_2_o1), .I0(reg_8bit_2_o0), .Clock(and_1_out),
    .Load(instruction_decoder_1_ra_in), .RST(RESET_out), .En(instruction_decoder_1_ra_out),
    .O7(reg_8bit_2_o7), .O6(reg_8bit_2_o6), .O5(reg_8bit_2_o5), .O4(reg_8bit_2_o4), .O3(reg_8bit_2_o3),
    .O2(reg_8bit_2_o2), .O1(reg_8bit_2_o1), .O0(reg_8bit_2_o0), .B7(reg_8bit_3_b7), .B6(reg_8bit_3_b6),
    .B5(reg_8bit_3_b5), .B4(reg_8bit_3_b4), .B3(reg_8bit_3_b3), .B2(reg_8bit_3_b2), .B1(reg_8bit_3_b1),
    .B0(reg_8bit_3_b0));
  LED led_1 (.in(instruction_decoder_1_ir_res));
  DotMatrix #(.dotshape("circle"), .matrixcols(8), .matrixrows(1)) dotmatrix_5 (
    .col0(reverser_2_s0), .col1(reverser_2_s1), .col2(reverser_2_s2), .col3(reverser_2_s3),
    .col4(reverser_2_s4), .col5(reverser_2_s5), .col6(reverser_2_s6), .col7(reverser_2_s7));
  Instruction_Decoder instruction_decoder_1 (
    .ZF(reg_2bit_1_o1), .CF(reg_2bit_1_o0), .CS0(reg_8bit_4_o0), .CS1(reg_8bit_4_o1), .CS2(reg_8bit_4_o2),
    .CS3(reg_8bit_4_o3), .CS4(reg_8bit_4_o4), .CS5(reg_8bit_4_o5), .Programming_Mode(Programming_Mode),
    .Clear(RESET_out), .Clock(and_1_out), .ALU_S0(instruction_decoder_1_alu_s0),
    .ALU_S1(instruction_decoder_1_alu_s1), .ALU_S2(instruction_decoder_1_alu_s2),
    .JP(instruction_decoder_1_jp), .C_out(instruction_decoder_1_c_out), .C_en(instruction_decoder_1_c_en),
    .IR_res(instruction_decoder_1_ir_res), .IR_in(instruction_decoder_1_ir_in),
    .RR(instruction_decoder_1_rr), .RW(instruction_decoder_1_rw), .MAR_in(instruction_decoder_1_mar_in),
    .RD_out(instruction_decoder_1_rd_out), .RD_in(instruction_decoder_1_rd_in),
    .RC_out(instruction_decoder_1_rc_out), .RC_in(instruction_decoder_1_rc_in),
    .RB_out(instruction_decoder_1_rb_out), .RB_in(instruction_decoder_1_rb_in),
    .RA_out(instruction_decoder_1_ra_out), .RA_in(instruction_decoder_1_ra_in),
    .Disp(instruction_decoder_1_disp), .ALU_out(instruction_decoder_1_alu_out),
    .Flags_in(instruction_decoder_1_flags_in), .Halt(instruction_decoder_1_halt),
    .S7(instruction_decoder_1_s7), .S6(instruction_decoder_1_s6), .S5(instruction_decoder_1_s5),
    .S4(instruction_decoder_1_s4), .S3(instruction_decoder_1_s3), .S2(instruction_decoder_1_s2),
    .S1(instruction_decoder_1_s1), .S0(instruction_decoder_1_s0));
  Reg_8bit reg_8bit_4 (
    .I7(reg_8bit_2_o7), .I6(reg_8bit_2_o6), .I5(reg_8bit_2_o5), .I4(reg_8bit_2_o4), .I3(reg_8bit_2_o3),
    .I2(reg_8bit_2_o2), .I1(reg_8bit_2_o1), .I0(reg_8bit_2_o0), .Clock(and_1_out),
    .Load(instruction_decoder_1_ir_in), .RST(RESET_out), .En(1'b1), .O5(reg_8bit_4_o5), .O4(reg_8bit_4_o4),
    .O3(reg_8bit_4_o3), .O2(reg_8bit_4_o2), .O1(reg_8bit_4_o1), .O0(reg_8bit_4_o0), .B7(reg_8bit_4_b7),
    .B6(reg_8bit_4_b6), .B5(reg_8bit_4_b5), .B4(reg_8bit_4_b4), .B3(reg_8bit_4_b3), .B2(reg_8bit_4_b2),
    .B1(reg_8bit_4_b1), .B0(reg_8bit_4_b0));  // open: O7, O6
  Reg_2bit reg_2bit_1 (
    .I1(alu_2_1_zf), .I0(alu_2_1_cf), .Clock(and_1_out), .Load(instruction_decoder_1_flags_in),
    .Rst(RESET_out), .En(1'b1), .B1(reg_2bit_1_b1), .B0(reg_2bit_1_b0), .O1(reg_2bit_1_o1), .O0(reg_2bit_1_o0));
  DotMatrix #(.dotshape("circle"), .matrixcols(2), .matrixrows(1)) dotmatrix_6 (
    .col0(reg_2bit_1_b1), .col1(reg_2bit_1_b0));
  DotMatrix #(.dotshape("circle"), .matrixcols(8), .matrixrows(1)) dotmatrix_7 (
    .col0(alu_2_1_s7), .col1(alu_2_1_s6), .col2(alu_2_1_s5), .col3(alu_2_1_s4), .col4(alu_2_1_s3),
    .col5(alu_2_1_s2), .col6(alu_2_1_s1), .col7(alu_2_1_s0));
  Reverser reverser_2 (
    .E0(reg_8bit_4_b0), .E1(reg_8bit_4_b1), .E2(reg_8bit_4_b2), .E3(reg_8bit_4_b3), .E4(reg_8bit_4_b4),
    .E5(reg_8bit_4_b5), .E6(reg_8bit_4_b6), .E7(reg_8bit_4_b7), .S7(reverser_2_s7), .S6(reverser_2_s6),
    .S5(reverser_2_s5), .S4(reverser_2_s4), .S3(reverser_2_s3), .S2(reverser_2_s2), .S1(reverser_2_s1),
    .S0(reverser_2_s0));
  ALU_2 alu_2_1 (
    .B7(reg_8bit_6_b7), .A7(reg_8bit_3_b7), .B6(reg_8bit_6_b6), .A6(reg_8bit_3_b6),
    .SE0(instruction_decoder_1_alu_s0), .B5(reg_8bit_6_b5), .A5(reg_8bit_3_b5), .B4(reg_8bit_6_b4),
    .A4(reg_8bit_3_b4), .SE1(instruction_decoder_1_alu_s1), .B3(reg_8bit_6_b3), .A3(reg_8bit_3_b3),
    .ALUo(instruction_decoder_1_alu_out), .B2(reg_8bit_6_b2), .A2(reg_8bit_3_b2),
    .SE2(instruction_decoder_1_alu_s2), .B1(reg_8bit_6_b1), .A1(reg_8bit_3_b1), .B0(reg_8bit_6_b0),
    .A0(reg_8bit_3_b0), .E7(reg_8bit_2_o7), .E6(reg_8bit_2_o6), .E5(reg_8bit_2_o5), .E4(reg_8bit_2_o4),
    .E3(reg_8bit_2_o3), .E2(reg_8bit_2_o2), .E1(reg_8bit_2_o1), .E0(reg_8bit_2_o0), .ZF(alu_2_1_zf),
    .CF(alu_2_1_cf), .S7(alu_2_1_s7), .S6(alu_2_1_s6), .S5(alu_2_1_s5), .S4(alu_2_1_s4), .S3(alu_2_1_s3),
    .S2(alu_2_1_s2), .S1(alu_2_1_s1), .S0(alu_2_1_s0));
  DotMatrix #(.dotshape("circle"), .matrixcols(8), .matrixrows(1)) dotmatrix_8 (
    .col0(reverser_3_s0), .col1(reverser_3_s1), .col2(reverser_3_s2), .col3(reverser_3_s3),
    .col4(reverser_3_s4), .col5(reverser_3_s5), .col6(reverser_3_s6), .col7(reverser_3_s7));
  Reg_8bit reg_8bit_5 (
    .I7(reg_8bit_2_o7), .I6(reg_8bit_2_o6), .I5(reg_8bit_2_o5), .I4(reg_8bit_2_o4), .I3(reg_8bit_2_o3),
    .I2(reg_8bit_2_o2), .I1(reg_8bit_2_o1), .I0(reg_8bit_2_o0), .Clock(and_1_out),
    .Load(instruction_decoder_1_rc_in), .RST(RESET_out), .En(instruction_decoder_1_rc_out),
    .O7(reg_8bit_2_o7), .O6(reg_8bit_2_o6), .O5(reg_8bit_2_o5), .O4(reg_8bit_2_o4), .O3(reg_8bit_2_o3),
    .O2(reg_8bit_2_o2), .O1(reg_8bit_2_o1), .O0(reg_8bit_2_o0), .B7(reg_8bit_5_b7), .B6(reg_8bit_5_b6),
    .B5(reg_8bit_5_b5), .B4(reg_8bit_5_b4), .B3(reg_8bit_5_b3), .B2(reg_8bit_5_b2), .B1(reg_8bit_5_b1),
    .B0(reg_8bit_5_b0));
  DotMatrix #(.dotshape("circle"), .matrixcols(8), .matrixrows(1)) dotmatrix_9 (
    .col0(reg_8bit_6_b7), .col1(reg_8bit_6_b6), .col2(reg_8bit_6_b5), .col3(reg_8bit_6_b4),
    .col4(reg_8bit_6_b3), .col5(reg_8bit_6_b2), .col6(reg_8bit_6_b1), .col7(reg_8bit_6_b0));
  // DotMatrix #(.dotshape("circle"), .inputtype("row"), .matrixcols(1), .matrixrows(8)) dotmatrix_10: pin names not known; wires that end beside it: dotmatrix_10_p1, dotmatrix_10_p2, dotmatrix_10_p3, dotmatrix_10_p4, dotmatrix_10_p5, dotmatrix_10_p6, dotmatrix_10_p7, dotmatrix_10_p8
  Reverser reverser_3 (
    .E0(reg_8bit_5_b0), .E1(reg_8bit_5_b1), .E2(reg_8bit_5_b2), .E3(reg_8bit_5_b3), .E4(reg_8bit_5_b4),
    .E5(reg_8bit_5_b5), .E6(reg_8bit_5_b6), .E7(reg_8bit_5_b7), .S7(reverser_3_s7), .S6(reverser_3_s6),
    .S5(reverser_3_s5), .S4(reverser_3_s4), .S3(reverser_3_s3), .S2(reverser_3_s2), .S1(reverser_3_s1),
    .S0(reverser_3_s0));
  Reg_8bit reg_8bit_6 (
    .I7(reg_8bit_2_o7), .I6(reg_8bit_2_o6), .I5(reg_8bit_2_o5), .I4(reg_8bit_2_o4), .I3(reg_8bit_2_o3),
    .I2(reg_8bit_2_o2), .I1(reg_8bit_2_o1), .I0(reg_8bit_2_o0), .Clock(and_1_out),
    .Load(instruction_decoder_1_rb_in), .RST(RESET_out), .En(instruction_decoder_1_rb_out),
    .O7(reg_8bit_2_o7), .O6(reg_8bit_2_o6), .O5(reg_8bit_2_o5), .O4(reg_8bit_2_o4), .O3(reg_8bit_2_o3),
    .O2(reg_8bit_2_o2), .O1(reg_8bit_2_o1), .O0(reg_8bit_2_o0), .B7(reg_8bit_6_b7), .B6(reg_8bit_6_b6),
    .B5(reg_8bit_6_b5), .B4(reg_8bit_6_b4), .B3(reg_8bit_6_b3), .B2(reg_8bit_6_b2), .B1(reg_8bit_6_b1),
    .B0(reg_8bit_6_b0));
  CPU_Counter cpu_counter_1 (
    .I7(reg_8bit_2_o7), .I6(reg_8bit_2_o6), .I5(reg_8bit_2_o5), .I4(reg_8bit_2_o4), .I3(reg_8bit_2_o3),
    .I2(reg_8bit_2_o2), .I1(reg_8bit_2_o1), .I0(reg_8bit_2_o0), .COut(instruction_decoder_1_c_out),
    .CEnable(instruction_decoder_1_c_en), .CWrite(instruction_decoder_1_jp), .CReset(RESET_out),
    .Clock(and_1_out), .O7(reg_8bit_2_o7), .O6(reg_8bit_2_o6), .O5(reg_8bit_2_o5), .O4(reg_8bit_2_o4),
    .O3(reg_8bit_2_o3), .O2(reg_8bit_2_o2), .O1(reg_8bit_2_o1), .O0(reg_8bit_2_o0), .D7(dotmatrix_10_p1),
    .D6(dotmatrix_10_p2), .D5(dotmatrix_10_p3), .D4(dotmatrix_10_p4), .D3(dotmatrix_10_p5),
    .D2(dotmatrix_10_p6), .D1(dotmatrix_10_p7), .D0(dotmatrix_10_p8));
  or or_1 (or_1_out, instruction_decoder_1_mar_in, program_loader_1_addr_write);
  DotMatrix #(.dotshape("circle"), .matrixcols(8), .matrixrows(1)) dotmatrix_11 (
    .col0(reg_8bit_7_b4[3]), .col1(reg_8bit_7_b4[2]), .col2(reg_8bit_7_b4[1]), .col3(reg_8bit_7_b4[0]),
    .col4(reg_8bit_7_b0[3]), .col5(reg_8bit_7_b0[2]), .col6(reg_8bit_7_b0[1]), .col7(reg_8bit_7_b0[0]));
  Hex_Digit_Display hex_digit_display_3 (.value(reg_8bit_7_b4));  // open: dp
  Hex_Digit_Display hex_digit_display_4 (.value(reg_8bit_7_b0));  // open: dp
  and and_1 (and_1_out, ~RESET_out, clock_1_out, ~instruction_decoder_1_halt);  // AND_Gate
  Reg_8bit reg_8bit_7 (
    .I7(reg_8bit_2_o7), .I6(reg_8bit_2_o6), .I5(reg_8bit_2_o5), .I4(reg_8bit_2_o4), .I3(reg_8bit_2_o3),
    .I2(reg_8bit_2_o2), .I1(reg_8bit_2_o1), .I0(reg_8bit_2_o0), .Clock(and_1_out), .Load(or_1_out),
    .RST(RESET_out), .En(1'b1), .O7(reg_8bit_7_o7), .O6(reg_8bit_7_o6), .O5(reg_8bit_7_o5),
    .O4(reg_8bit_7_o4), .O3(reg_8bit_7_o3), .O2(reg_8bit_7_o2), .O1(reg_8bit_7_o1), .O0(reg_8bit_7_o0),
    .B7(reg_8bit_7_b4[3]), .B6(reg_8bit_7_b4[2]), .B5(reg_8bit_7_b4[1]), .B4(reg_8bit_7_b4[0]),
    .B3(reg_8bit_7_b0[3]), .B2(reg_8bit_7_b0[2]), .B1(reg_8bit_7_b0[1]), .B0(reg_8bit_7_b0[0]));
  DotMatrix #(.dotshape("circle"), .matrixcols(8), .matrixrows(1)) dotmatrix_12 (
    .col0(reg_8bit_2_o7), .col1(reg_8bit_2_o6), .col2(reg_8bit_2_o5), .col3(reg_8bit_2_o4),
    .col4(reg_8bit_2_o3), .col5(reg_8bit_2_o2), .col6(reg_8bit_2_o1), .col7(reg_8bit_2_o0));
  Hex_Digit_Display hex_digit_display_5 (.value(sram_256_bytes_1_s4));  // open: dp
  Hex_Digit_Display hex_digit_display_6 (.value(sram_256_bytes_1_s0));  // open: dp
  Program_Loader program_loader_1 (
    .Enable(Programming_Mode), .ROM_Data(rom_1_data), .Clock(and_1_out), .Reset(RESET_out),
    .ROM_Addr(program_loader_1_rom_addr), .O4(reg_8bit_2_o4), .O3(reg_8bit_2_o3), .O2(reg_8bit_2_o2),
    .O1(reg_8bit_2_o1), .O0(reg_8bit_2_o0), .Programming(program_loader_1_programming),
    .Addr_Write(program_loader_1_addr_write), .RAM_Write(program_loader_1_ram_write), .O7(reg_8bit_2_o7),
    .O6(reg_8bit_2_o6), .O5(reg_8bit_2_o5));
  or or_2 (or_2_out, instruction_decoder_1_rw, program_loader_1_ram_write);
  SRAM_256_bytes sram_256_bytes_1 (
    .I7(reg_8bit_2_o7), .I6(reg_8bit_2_o6), .I5(reg_8bit_2_o5), .I4(reg_8bit_2_o4), .I3(reg_8bit_2_o3),
    .I2(reg_8bit_2_o2), .I1(reg_8bit_2_o1), .I0(reg_8bit_2_o0), .Read(instruction_decoder_1_rr),
    .Write(or_2_out), .Clear(RST_RAM_out), .Clock(and_1_out), .A7(reg_8bit_7_o7), .A6(reg_8bit_7_o6),
    .A5(reg_8bit_7_o5), .A4(reg_8bit_7_o4), .A3(reg_8bit_7_o3), .A2(reg_8bit_7_o2), .A1(reg_8bit_7_o1),
    .A0(reg_8bit_7_o0), .S7(sram_256_bytes_1_s4[3]), .S6(sram_256_bytes_1_s4[2]),
    .S5(sram_256_bytes_1_s4[1]), .S4(sram_256_bytes_1_s4[0]), .S3(sram_256_bytes_1_s0[3]),
    .S2(sram_256_bytes_1_s0[2]), .S1(sram_256_bytes_1_s0[1]), .S0(sram_256_bytes_1_s0[0]),
    .O7(reg_8bit_2_o7), .O6(reg_8bit_2_o6), .O5(reg_8bit_2_o5), .O4(reg_8bit_2_o4), .O3(reg_8bit_2_o3),
    .O2(reg_8bit_2_o2), .O1(reg_8bit_2_o1), .O0(reg_8bit_2_o0));
  Clock clock_1 (.out(clock_1_out));
  Button RST_RAM (.out(RST_RAM_out));
  Button RESET (.out(RESET_out));
  ROM rom_1 (.addr(program_loader_1_rom_addr), .data(rom_1_data));
  _7_Segment_Display u_7_segment_display_1 (
    .g(decoder_8_bits_to_7_segment_1_g3), .f(decoder_8_bits_to_7_segment_1_f3),
    .a(decoder_8_bits_to_7_segment_1_a3), .b(decoder_8_bits_to_7_segment_1_b3),
    .e(decoder_8_bits_to_7_segment_1_e3), .d(decoder_8_bits_to_7_segment_1_d3),
    .c(decoder_8_bits_to_7_segment_1_c3));  // open: dp
  _7_Segment_Display u_7_segment_display_2 (
    .g(decoder_8_bits_to_7_segment_1_g2), .f(decoder_8_bits_to_7_segment_1_f2),
    .a(decoder_8_bits_to_7_segment_1_a2), .b(decoder_8_bits_to_7_segment_1_b2),
    .e(decoder_8_bits_to_7_segment_1_e2), .d(decoder_8_bits_to_7_segment_1_d2),
    .c(decoder_8_bits_to_7_segment_1_c2));  // open: dp
  LED led_2 (.in(program_loader_1_programming));
  _7_Segment_Display u_7_segment_display_3 (
    .g(decoder_8_bits_to_7_segment_1_g1), .f(decoder_8_bits_to_7_segment_1_f1),
    .a(decoder_8_bits_to_7_segment_1_a1), .b(decoder_8_bits_to_7_segment_1_b1),
    .e(decoder_8_bits_to_7_segment_1_e1), .d(decoder_8_bits_to_7_segment_1_d1),
    .c(decoder_8_bits_to_7_segment_1_c1));  // open: dp
  Decoder_8_bits_to_7_segment decoder_8_bits_to_7_segment_1 (
    .in_1({reg_8bit_1_b3, reg_8bit_1_b7}), .d1(decoder_8_bits_to_7_segment_1_d1),
    .e1(decoder_8_bits_to_7_segment_1_e1), .f1(decoder_8_bits_to_7_segment_1_f1),
    .g1(decoder_8_bits_to_7_segment_1_g1), .a2(decoder_8_bits_to_7_segment_1_a2),
    .b2(decoder_8_bits_to_7_segment_1_b2), .c2(decoder_8_bits_to_7_segment_1_c2),
    .d2(decoder_8_bits_to_7_segment_1_d2), .e2(decoder_8_bits_to_7_segment_1_e2),
    .f2(decoder_8_bits_to_7_segment_1_f2), .g2(decoder_8_bits_to_7_segment_1_g2),
    .a3(decoder_8_bits_to_7_segment_1_a3), .b3(decoder_8_bits_to_7_segment_1_b3),
    .c3(decoder_8_bits_to_7_segment_1_c3), .d3(decoder_8_bits_to_7_segment_1_d3),
    .e3(decoder_8_bits_to_7_segment_1_e3), .f3(decoder_8_bits_to_7_segment_1_f3),
    .g3(decoder_8_bits_to_7_segment_1_g3), .a1(decoder_8_bits_to_7_segment_1_a1),
    .b1(decoder_8_bits_to_7_segment_1_b1), .c1(decoder_8_bits_to_7_segment_1_c1));

  // Notes on the sheet:
  //   Display
  //   D
  //   A
  //   Instruction
  //   Register
  //   C
  //   B
  //   Memory
  //   Register
  //   contents of rom_1 (hex, n*v repeats v):
  //   2 0 5 1 1f d 0 9 0 10 0 1f 14 5 1
endmodule
module Processor (
  input  Programming_Mode
);

  wire alu_2_1_cf, alu_2_1_s0, alu_2_1_s1, alu_2_1_s2, alu_2_1_s3, alu_2_1_s4, alu_2_1_s5, alu_2_1_s6,
       alu_2_1_s7, alu_2_1_zf, and_1_out, clock_1_out, decoder_8_bits_to_7_segment_1_a1,
       decoder_8_bits_to_7_segment_1_a2, decoder_8_bits_to_7_segment_1_a3, decoder_8_bits_to_7_segment_1_b1,
       decoder_8_bits_to_7_segment_1_b2, decoder_8_bits_to_7_segment_1_b3, decoder_8_bits_to_7_segment_1_c1,
       decoder_8_bits_to_7_segment_1_c2, decoder_8_bits_to_7_segment_1_c3, decoder_8_bits_to_7_segment_1_d1,
       decoder_8_bits_to_7_segment_1_d2, decoder_8_bits_to_7_segment_1_d3, decoder_8_bits_to_7_segment_1_e1,
       decoder_8_bits_to_7_segment_1_e2, decoder_8_bits_to_7_segment_1_e3, decoder_8_bits_to_7_segment_1_f1,
       decoder_8_bits_to_7_segment_1_f2, decoder_8_bits_to_7_segment_1_f3, decoder_8_bits_to_7_segment_1_g1,
       decoder_8_bits_to_7_segment_1_g2, decoder_8_bits_to_7_segment_1_g3, dotmatrix_9_p1, dotmatrix_9_p2,
       dotmatrix_9_p3, dotmatrix_9_p4, dotmatrix_9_p5, dotmatrix_9_p6, dotmatrix_9_p7, dotmatrix_9_p8,
       instruction_decoder_1_alu_out, instruction_decoder_1_alu_s0, instruction_decoder_1_alu_s1,
       instruction_decoder_1_alu_s2, instruction_decoder_1_c_en, instruction_decoder_1_c_out,
       instruction_decoder_1_disp, instruction_decoder_1_flags_in, instruction_decoder_1_halt,
       instruction_decoder_1_ir_in, instruction_decoder_1_ir_res, instruction_decoder_1_jp,
       instruction_decoder_1_mar_in, instruction_decoder_1_ra_in, instruction_decoder_1_ra_out,
       instruction_decoder_1_rb_in, instruction_decoder_1_rb_out, instruction_decoder_1_rc_in,
       instruction_decoder_1_rc_out, instruction_decoder_1_rd_in, instruction_decoder_1_rd_out,
       instruction_decoder_1_rr, instruction_decoder_1_rw, instruction_decoder_1_s0,
       instruction_decoder_1_s1, instruction_decoder_1_s2, instruction_decoder_1_s3,
       instruction_decoder_1_s4, instruction_decoder_1_s5, instruction_decoder_1_s6,
       instruction_decoder_1_s7, or_1_out, or_2_out, program_loader_1_addr_write,
       program_loader_1_programming, program_loader_1_ram_write, reg_2bit_1_b0, reg_2bit_1_b1, reg_2bit_1_o0,
       reg_2bit_1_o1, reg_8bit_1_b0, reg_8bit_1_b1, reg_8bit_1_b2, reg_8bit_1_b3, reg_8bit_1_b4,
       reg_8bit_1_b5, reg_8bit_1_b6, reg_8bit_1_b7, reg_8bit_1_o0, reg_8bit_1_o1, reg_8bit_1_o2,
       reg_8bit_1_o3, reg_8bit_1_o4, reg_8bit_1_o5, reg_8bit_1_o6, reg_8bit_1_o7, reg_8bit_3_b0,
       reg_8bit_3_b1, reg_8bit_3_b2, reg_8bit_3_b3, reg_8bit_3_b4, reg_8bit_3_b5, reg_8bit_3_b6,
       reg_8bit_3_b7, reg_8bit_4_b0, reg_8bit_4_b1, reg_8bit_4_b2, reg_8bit_4_b3, reg_8bit_4_b4,
       reg_8bit_4_b5, reg_8bit_4_b6, reg_8bit_4_b7, reg_8bit_4_o0, reg_8bit_4_o1, reg_8bit_4_o2,
       reg_8bit_4_o3, reg_8bit_4_o4, reg_8bit_4_o5, reg_8bit_5_b0, reg_8bit_5_b1, reg_8bit_5_b2,
       reg_8bit_5_b3, reg_8bit_5_b4, reg_8bit_5_b5, reg_8bit_5_b6, reg_8bit_5_b7, reg_8bit_6_b0,
       reg_8bit_6_b1, reg_8bit_6_b2, reg_8bit_6_b3, reg_8bit_6_b4, reg_8bit_6_b5, reg_8bit_6_b6,
       reg_8bit_6_b7, reg_8bit_7_o0, reg_8bit_7_o1, reg_8bit_7_o2, reg_8bit_7_o3, reg_8bit_7_o4,
       reg_8bit_7_o5, reg_8bit_7_o6, reg_8bit_7_o7, RESET_out, reverser_1_s0, reverser_1_s1, reverser_1_s2,
       reverser_1_s3, reverser_1_s4, reverser_1_s5, reverser_1_s6, reverser_1_s7, reverser_2_s0,
       reverser_2_s1, reverser_2_s2, reverser_2_s3, reverser_2_s4, reverser_2_s5, reverser_2_s6,
       reverser_2_s7, RST_RAM_out;
  wire [3:0] reg_8bit_7_b0, reg_8bit_7_b4, sram_256_bytes_1_s0, sram_256_bytes_1_s4;
  wire [7:0] program_loader_1_rom_addr, reg_8bit_2_b7, rom_1_data;

  Reg_8bit reg_8bit_1 (
    .I7(reg_8bit_1_o7), .I6(reg_8bit_1_o6), .I5(reg_8bit_1_o5), .I4(reg_8bit_1_o4), .I3(reg_8bit_1_o3),
    .I2(reg_8bit_1_o2), .I1(reg_8bit_1_o1), .I0(reg_8bit_1_o0), .Clock(and_1_out),
    .Load(instruction_decoder_1_rd_in), .RST(RESET_out), .En(instruction_decoder_1_rd_out),
    .O7(reg_8bit_1_o7), .O6(reg_8bit_1_o6), .O5(reg_8bit_1_o5), .O4(reg_8bit_1_o4), .O3(reg_8bit_1_o3),
    .O2(reg_8bit_1_o2), .O1(reg_8bit_1_o1), .O0(reg_8bit_1_o0), .B7(reg_8bit_1_b7), .B6(reg_8bit_1_b6),
    .B5(reg_8bit_1_b5), .B4(reg_8bit_1_b4), .B3(reg_8bit_1_b3), .B2(reg_8bit_1_b2), .B1(reg_8bit_1_b1),
    .B0(reg_8bit_1_b0));
  Reg_8bit reg_8bit_2 (
    .I7(reg_8bit_1_o0), .I6(reg_8bit_1_o1), .I5(reg_8bit_1_o2), .I4(reg_8bit_1_o3), .I3(reg_8bit_1_o4),
    .I2(reg_8bit_1_o5), .I1(reg_8bit_1_o6), .I0(reg_8bit_1_o7), .Clock(and_1_out),
    .Load(instruction_decoder_1_disp), .RST(RESET_out), .En(1'b1), .B7(reg_8bit_2_b7[0]),
    .B6(reg_8bit_2_b7[1]), .B5(reg_8bit_2_b7[2]), .B4(reg_8bit_2_b7[3]), .B3(reg_8bit_2_b7[4]),
    .B2(reg_8bit_2_b7[5]), .B1(reg_8bit_2_b7[6]), .B0(reg_8bit_2_b7[7]));  // open: O7, O6, O5, O4, O3, O2, O1, O0
  DotMatrix #(.dotshape("circle"), .inputtype("row"), .matrixcols(1), .matrixrows(8)) dotmatrix_1 (
    .row0(reverser_1_s0), .row1(reverser_1_s1), .row2(reverser_1_s2), .row3(reverser_1_s3),
    .row4(reverser_1_s4), .row5(reverser_1_s5), .row6(reverser_1_s6), .row7(reverser_1_s7));
  Reverser reverser_1 (
    .E0(reg_8bit_1_b0), .E1(reg_8bit_1_b1), .E2(reg_8bit_1_b2), .E3(reg_8bit_1_b3), .E4(reg_8bit_1_b4),
    .E5(reg_8bit_1_b5), .E6(reg_8bit_1_b6), .E7(reg_8bit_1_b7), .S7(reverser_1_s7), .S6(reverser_1_s6),
    .S5(reverser_1_s5), .S4(reverser_1_s4), .S3(reverser_1_s3), .S2(reverser_1_s2), .S1(reverser_1_s1),
    .S0(reverser_1_s0));
  DotMatrix #(.dotshape("circle"), .matrixcols(8), .matrixrows(1)) dotmatrix_2 (
    .col0(instruction_decoder_1_s7), .col1(instruction_decoder_1_s6), .col2(instruction_decoder_1_s5),
    .col3(instruction_decoder_1_s4), .col4(instruction_decoder_1_s3), .col5(instruction_decoder_1_s2),
    .col6(instruction_decoder_1_s1), .col7(instruction_decoder_1_s0));
  DotMatrix #(.dotshape("circle"), .matrixcols(8), .matrixrows(1)) dotmatrix_3 (
    .col0(reg_8bit_3_b7), .col1(reg_8bit_3_b6), .col2(reg_8bit_3_b5), .col3(reg_8bit_3_b4),
    .col4(reg_8bit_3_b3), .col5(reg_8bit_3_b2), .col6(reg_8bit_3_b1), .col7(reg_8bit_3_b0));
  Reg_8bit reg_8bit_3 (
    .I7(reg_8bit_1_o7), .I6(reg_8bit_1_o6), .I5(reg_8bit_1_o5), .I4(reg_8bit_1_o4), .I3(reg_8bit_1_o3),
    .I2(reg_8bit_1_o2), .I1(reg_8bit_1_o1), .I0(reg_8bit_1_o0), .Clock(and_1_out),
    .Load(instruction_decoder_1_ra_in), .RST(RESET_out), .En(instruction_decoder_1_ra_out),
    .O7(reg_8bit_1_o7), .O6(reg_8bit_1_o6), .O5(reg_8bit_1_o5), .O4(reg_8bit_1_o4), .O3(reg_8bit_1_o3),
    .O2(reg_8bit_1_o2), .O1(reg_8bit_1_o1), .O0(reg_8bit_1_o0), .B7(reg_8bit_3_b7), .B6(reg_8bit_3_b6),
    .B5(reg_8bit_3_b5), .B4(reg_8bit_3_b4), .B3(reg_8bit_3_b3), .B2(reg_8bit_3_b2), .B1(reg_8bit_3_b1),
    .B0(reg_8bit_3_b0));
  LED led_1 (.in(instruction_decoder_1_ir_res));
  Instruction_Decoder instruction_decoder_1 (
    .ZF(reg_2bit_1_o1), .CF(reg_2bit_1_o0), .CS0(reg_8bit_4_o0), .CS1(reg_8bit_4_o1), .CS2(reg_8bit_4_o2),
    .CS3(reg_8bit_4_o3), .CS4(reg_8bit_4_o4), .CS5(reg_8bit_4_o5), .Programming_Mode(Programming_Mode),
    .Clear(RESET_out), .Clock(and_1_out), .ALU_S0(instruction_decoder_1_alu_s0),
    .ALU_S1(instruction_decoder_1_alu_s1), .ALU_S2(instruction_decoder_1_alu_s2),
    .JP(instruction_decoder_1_jp), .C_out(instruction_decoder_1_c_out), .C_en(instruction_decoder_1_c_en),
    .IR_res(instruction_decoder_1_ir_res), .IR_in(instruction_decoder_1_ir_in),
    .RR(instruction_decoder_1_rr), .RW(instruction_decoder_1_rw), .MAR_in(instruction_decoder_1_mar_in),
    .RD_out(instruction_decoder_1_rd_out), .RD_in(instruction_decoder_1_rd_in),
    .RC_out(instruction_decoder_1_rc_out), .RC_in(instruction_decoder_1_rc_in),
    .RB_out(instruction_decoder_1_rb_out), .RB_in(instruction_decoder_1_rb_in),
    .RA_out(instruction_decoder_1_ra_out), .RA_in(instruction_decoder_1_ra_in),
    .Disp(instruction_decoder_1_disp), .ALU_out(instruction_decoder_1_alu_out),
    .Flags_in(instruction_decoder_1_flags_in), .Halt(instruction_decoder_1_halt),
    .S7(instruction_decoder_1_s7), .S6(instruction_decoder_1_s6), .S5(instruction_decoder_1_s5),
    .S4(instruction_decoder_1_s4), .S3(instruction_decoder_1_s3), .S2(instruction_decoder_1_s2),
    .S1(instruction_decoder_1_s1), .S0(instruction_decoder_1_s0));
  Reg_2bit reg_2bit_1 (
    .I1(alu_2_1_zf), .I0(alu_2_1_cf), .Clock(and_1_out), .Load(instruction_decoder_1_flags_in),
    .Rst(RESET_out), .En(1'b1), .B1(reg_2bit_1_b1), .B0(reg_2bit_1_b0), .O1(reg_2bit_1_o1), .O0(reg_2bit_1_o0));
  DotMatrix #(.dotshape("circle"), .matrixcols(2), .matrixrows(1)) dotmatrix_4 (
    .col0(reg_2bit_1_b1), .col1(reg_2bit_1_b0));
  DotMatrix #(.dotshape("circle"), .matrixcols(8), .matrixrows(1)) dotmatrix_5 (
    .col0(alu_2_1_s7), .col1(alu_2_1_s6), .col2(alu_2_1_s5), .col3(alu_2_1_s4), .col4(alu_2_1_s3),
    .col5(alu_2_1_s2), .col6(alu_2_1_s1), .col7(alu_2_1_s0));
  DotMatrix #(.dotshape("circle"), .matrixcols(8), .matrixrows(1)) dotmatrix_6 (
    .col0(reverser_2_s0), .col1(reverser_2_s1), .col2(reverser_2_s2), .col3(reverser_2_s3),
    .col4(reverser_2_s4), .col5(reverser_2_s5), .col6(reverser_2_s6), .col7(reverser_2_s7));
  Reg_8bit reg_8bit_4 (
    .I7(reg_8bit_1_o7), .I6(reg_8bit_1_o6), .I5(reg_8bit_1_o5), .I4(reg_8bit_1_o4), .I3(reg_8bit_1_o3),
    .I2(reg_8bit_1_o2), .I1(reg_8bit_1_o1), .I0(reg_8bit_1_o0), .Clock(and_1_out),
    .Load(instruction_decoder_1_ir_in), .RST(RESET_out), .En(1'b1), .O5(reg_8bit_4_o5), .O4(reg_8bit_4_o4),
    .O3(reg_8bit_4_o3), .O2(reg_8bit_4_o2), .O1(reg_8bit_4_o1), .O0(reg_8bit_4_o0), .B7(reg_8bit_4_b7),
    .B6(reg_8bit_4_b6), .B5(reg_8bit_4_b5), .B4(reg_8bit_4_b4), .B3(reg_8bit_4_b3), .B2(reg_8bit_4_b2),
    .B1(reg_8bit_4_b1), .B0(reg_8bit_4_b0));  // open: O7, O6
  ALU_2 alu_2_1 (
    .B7(reg_8bit_6_b7), .A7(reg_8bit_3_b7), .B6(reg_8bit_6_b6), .A6(reg_8bit_3_b6),
    .SE0(instruction_decoder_1_alu_s0), .B5(reg_8bit_6_b5), .A5(reg_8bit_3_b5), .B4(reg_8bit_6_b4),
    .A4(reg_8bit_3_b4), .SE1(instruction_decoder_1_alu_s1), .B3(reg_8bit_6_b3), .A3(reg_8bit_3_b3),
    .ALUo(instruction_decoder_1_alu_out), .B2(reg_8bit_6_b2), .A2(reg_8bit_3_b2),
    .SE2(instruction_decoder_1_alu_s2), .B1(reg_8bit_6_b1), .A1(reg_8bit_3_b1), .B0(reg_8bit_6_b0),
    .A0(reg_8bit_3_b0), .E7(reg_8bit_1_o7), .E6(reg_8bit_1_o6), .E5(reg_8bit_1_o5), .E4(reg_8bit_1_o4),
    .E3(reg_8bit_1_o3), .E2(reg_8bit_1_o2), .E1(reg_8bit_1_o1), .E0(reg_8bit_1_o0), .ZF(alu_2_1_zf),
    .CF(alu_2_1_cf), .S7(alu_2_1_s7), .S6(alu_2_1_s6), .S5(alu_2_1_s5), .S4(alu_2_1_s4), .S3(alu_2_1_s3),
    .S2(alu_2_1_s2), .S1(alu_2_1_s1), .S0(alu_2_1_s0));
  Reverser reverser_2 (
    .E0(reg_8bit_4_b0), .E1(reg_8bit_4_b1), .E2(reg_8bit_4_b2), .E3(reg_8bit_4_b3), .E4(reg_8bit_4_b4),
    .E5(reg_8bit_4_b5), .E6(reg_8bit_4_b6), .E7(reg_8bit_4_b7), .S7(reverser_2_s7), .S6(reverser_2_s6),
    .S5(reverser_2_s5), .S4(reverser_2_s4), .S3(reverser_2_s3), .S2(reverser_2_s2), .S1(reverser_2_s1),
    .S0(reverser_2_s0));
  DotMatrix #(.dotshape("circle"), .matrixcols(8), .matrixrows(1)) dotmatrix_7 (
    .col0(reg_8bit_5_b7), .col1(reg_8bit_5_b6), .col2(reg_8bit_5_b5), .col3(reg_8bit_5_b4),
    .col4(reg_8bit_5_b3), .col5(reg_8bit_5_b2), .col6(reg_8bit_5_b1), .col7(reg_8bit_5_b0));
  DotMatrix #(.dotshape("circle"), .matrixcols(8), .matrixrows(1)) dotmatrix_8 (
    .col0(reg_8bit_6_b7), .col1(reg_8bit_6_b6), .col2(reg_8bit_6_b5), .col3(reg_8bit_6_b4),
    .col4(reg_8bit_6_b3), .col5(reg_8bit_6_b2), .col6(reg_8bit_6_b1), .col7(reg_8bit_6_b0));
  // DotMatrix #(.dotshape("circle"), .inputtype("row"), .matrixcols(1), .matrixrows(8)) dotmatrix_9: pin names not known; wires that end beside it: dotmatrix_9_p1, dotmatrix_9_p2, dotmatrix_9_p3, dotmatrix_9_p4, dotmatrix_9_p5, dotmatrix_9_p6, dotmatrix_9_p7, dotmatrix_9_p8
  Reg_8bit reg_8bit_5 (
    .I7(reg_8bit_1_o7), .I6(reg_8bit_1_o6), .I5(reg_8bit_1_o5), .I4(reg_8bit_1_o4), .I3(reg_8bit_1_o3),
    .I2(reg_8bit_1_o2), .I1(reg_8bit_1_o1), .I0(reg_8bit_1_o0), .Clock(and_1_out),
    .Load(instruction_decoder_1_rc_in), .RST(RESET_out), .En(instruction_decoder_1_rc_out),
    .O7(reg_8bit_1_o7), .O6(reg_8bit_1_o6), .O5(reg_8bit_1_o5), .O4(reg_8bit_1_o4), .O3(reg_8bit_1_o3),
    .O2(reg_8bit_1_o2), .O1(reg_8bit_1_o1), .O0(reg_8bit_1_o0), .B7(reg_8bit_5_b7), .B6(reg_8bit_5_b6),
    .B5(reg_8bit_5_b5), .B4(reg_8bit_5_b4), .B3(reg_8bit_5_b3), .B2(reg_8bit_5_b2), .B1(reg_8bit_5_b1),
    .B0(reg_8bit_5_b0));
  Reg_8bit reg_8bit_6 (
    .I7(reg_8bit_1_o7), .I6(reg_8bit_1_o6), .I5(reg_8bit_1_o5), .I4(reg_8bit_1_o4), .I3(reg_8bit_1_o3),
    .I2(reg_8bit_1_o2), .I1(reg_8bit_1_o1), .I0(reg_8bit_1_o0), .Clock(and_1_out),
    .Load(instruction_decoder_1_rb_in), .RST(RESET_out), .En(instruction_decoder_1_rb_out),
    .O7(reg_8bit_1_o7), .O6(reg_8bit_1_o6), .O5(reg_8bit_1_o5), .O4(reg_8bit_1_o4), .O3(reg_8bit_1_o3),
    .O2(reg_8bit_1_o2), .O1(reg_8bit_1_o1), .O0(reg_8bit_1_o0), .B7(reg_8bit_6_b7), .B6(reg_8bit_6_b6),
    .B5(reg_8bit_6_b5), .B4(reg_8bit_6_b4), .B3(reg_8bit_6_b3), .B2(reg_8bit_6_b2), .B1(reg_8bit_6_b1),
    .B0(reg_8bit_6_b0));
  CPU_Counter cpu_counter_1 (
    .I7(reg_8bit_1_o7), .I6(reg_8bit_1_o6), .I5(reg_8bit_1_o5), .I4(reg_8bit_1_o4), .I3(reg_8bit_1_o3),
    .I2(reg_8bit_1_o2), .I1(reg_8bit_1_o1), .I0(reg_8bit_1_o0), .COut(instruction_decoder_1_c_out),
    .CEnable(instruction_decoder_1_c_en), .CWrite(instruction_decoder_1_jp), .CReset(RESET_out),
    .Clock(and_1_out), .O7(reg_8bit_1_o7), .O6(reg_8bit_1_o6), .O5(reg_8bit_1_o5), .O4(reg_8bit_1_o4),
    .O3(reg_8bit_1_o3), .O2(reg_8bit_1_o2), .O1(reg_8bit_1_o1), .O0(reg_8bit_1_o0), .D7(dotmatrix_9_p1),
    .D6(dotmatrix_9_p2), .D5(dotmatrix_9_p3), .D4(dotmatrix_9_p4), .D3(dotmatrix_9_p5), .D2(dotmatrix_9_p6),
    .D1(dotmatrix_9_p7), .D0(dotmatrix_9_p8));
  or or_1 (or_1_out, instruction_decoder_1_mar_in, program_loader_1_addr_write);
  DotMatrix #(.dotshape("circle"), .matrixcols(8), .matrixrows(1)) dotmatrix_10 (
    .col0(reg_8bit_7_b4[3]), .col1(reg_8bit_7_b4[2]), .col2(reg_8bit_7_b4[1]), .col3(reg_8bit_7_b4[0]),
    .col4(reg_8bit_7_b0[3]), .col5(reg_8bit_7_b0[2]), .col6(reg_8bit_7_b0[1]), .col7(reg_8bit_7_b0[0]));
  Hex_Digit_Display hex_digit_display_1 (.value(reg_8bit_7_b4));  // open: dp
  Hex_Digit_Display hex_digit_display_2 (.value(reg_8bit_7_b0));  // open: dp
  and and_1 (and_1_out, ~RESET_out, clock_1_out, ~instruction_decoder_1_halt);  // AND_Gate
  Reg_8bit reg_8bit_7 (
    .I7(reg_8bit_1_o7), .I6(reg_8bit_1_o6), .I5(reg_8bit_1_o5), .I4(reg_8bit_1_o4), .I3(reg_8bit_1_o3),
    .I2(reg_8bit_1_o2), .I1(reg_8bit_1_o1), .I0(reg_8bit_1_o0), .Clock(and_1_out), .Load(or_1_out),
    .RST(RESET_out), .En(1'b1), .O7(reg_8bit_7_o7), .O6(reg_8bit_7_o6), .O5(reg_8bit_7_o5),
    .O4(reg_8bit_7_o4), .O3(reg_8bit_7_o3), .O2(reg_8bit_7_o2), .O1(reg_8bit_7_o1), .O0(reg_8bit_7_o0),
    .B7(reg_8bit_7_b4[3]), .B6(reg_8bit_7_b4[2]), .B5(reg_8bit_7_b4[1]), .B4(reg_8bit_7_b4[0]),
    .B3(reg_8bit_7_b0[3]), .B2(reg_8bit_7_b0[2]), .B1(reg_8bit_7_b0[1]), .B0(reg_8bit_7_b0[0]));
  DotMatrix #(.dotshape("circle"), .matrixcols(8), .matrixrows(1)) dotmatrix_11 (
    .col0(reg_8bit_1_o7), .col1(reg_8bit_1_o6), .col2(reg_8bit_1_o5), .col3(reg_8bit_1_o4),
    .col4(reg_8bit_1_o3), .col5(reg_8bit_1_o2), .col6(reg_8bit_1_o1), .col7(reg_8bit_1_o0));
  Hex_Digit_Display hex_digit_display_3 (.value(sram_256_bytes_1_s4));  // open: dp
  Hex_Digit_Display hex_digit_display_4 (.value(sram_256_bytes_1_s0));  // open: dp
  Program_Loader program_loader_1 (
    .Enable(Programming_Mode), .ROM_Data(rom_1_data), .Clock(and_1_out), .Reset(RESET_out),
    .ROM_Addr(program_loader_1_rom_addr), .O4(reg_8bit_1_o4), .O3(reg_8bit_1_o3), .O2(reg_8bit_1_o2),
    .O1(reg_8bit_1_o1), .O0(reg_8bit_1_o0), .Programming(program_loader_1_programming),
    .Addr_Write(program_loader_1_addr_write), .RAM_Write(program_loader_1_ram_write), .O7(reg_8bit_1_o7),
    .O6(reg_8bit_1_o6), .O5(reg_8bit_1_o5));
  or or_2 (or_2_out, instruction_decoder_1_rw, program_loader_1_ram_write);
  SRAM_256_bytes sram_256_bytes_1 (
    .I7(reg_8bit_1_o7), .I6(reg_8bit_1_o6), .I5(reg_8bit_1_o5), .I4(reg_8bit_1_o4), .I3(reg_8bit_1_o3),
    .I2(reg_8bit_1_o2), .I1(reg_8bit_1_o1), .I0(reg_8bit_1_o0), .Read(instruction_decoder_1_rr),
    .Write(or_2_out), .Clear(RST_RAM_out), .Clock(and_1_out), .A7(reg_8bit_7_o7), .A6(reg_8bit_7_o6),
    .A5(reg_8bit_7_o5), .A4(reg_8bit_7_o4), .A3(reg_8bit_7_o3), .A2(reg_8bit_7_o2), .A1(reg_8bit_7_o1),
    .A0(reg_8bit_7_o0), .S7(sram_256_bytes_1_s4[3]), .S6(sram_256_bytes_1_s4[2]),
    .S5(sram_256_bytes_1_s4[1]), .S4(sram_256_bytes_1_s4[0]), .S3(sram_256_bytes_1_s0[3]),
    .S2(sram_256_bytes_1_s0[2]), .S1(sram_256_bytes_1_s0[1]), .S0(sram_256_bytes_1_s0[0]),
    .O7(reg_8bit_1_o7), .O6(reg_8bit_1_o6), .O5(reg_8bit_1_o5), .O4(reg_8bit_1_o4), .O3(reg_8bit_1_o3),
    .O2(reg_8bit_1_o2), .O1(reg_8bit_1_o1), .O0(reg_8bit_1_o0));
  Clock clock_1 (.out(clock_1_out));
  Button RST_RAM (.out(RST_RAM_out));
  Button RESET (.out(RESET_out));
  ROM rom_1 (.addr(program_loader_1_rom_addr), .data(rom_1_data));
  _7_Segment_Display u_7_segment_display_1 (
    .g(decoder_8_bits_to_7_segment_1_g3), .f(decoder_8_bits_to_7_segment_1_f3),
    .a(decoder_8_bits_to_7_segment_1_a3), .b(decoder_8_bits_to_7_segment_1_b3),
    .e(decoder_8_bits_to_7_segment_1_e3), .d(decoder_8_bits_to_7_segment_1_d3),
    .c(decoder_8_bits_to_7_segment_1_c3));  // open: dp
  LED led_2 (.in(program_loader_1_programming));
  _7_Segment_Display u_7_segment_display_2 (
    .g(decoder_8_bits_to_7_segment_1_g2), .f(decoder_8_bits_to_7_segment_1_f2),
    .a(decoder_8_bits_to_7_segment_1_a2), .b(decoder_8_bits_to_7_segment_1_b2),
    .e(decoder_8_bits_to_7_segment_1_e2), .d(decoder_8_bits_to_7_segment_1_d2),
    .c(decoder_8_bits_to_7_segment_1_c2));  // open: dp
  _7_Segment_Display u_7_segment_display_3 (
    .g(decoder_8_bits_to_7_segment_1_g1), .f(decoder_8_bits_to_7_segment_1_f1),
    .a(decoder_8_bits_to_7_segment_1_a1), .b(decoder_8_bits_to_7_segment_1_b1),
    .e(decoder_8_bits_to_7_segment_1_e1), .d(decoder_8_bits_to_7_segment_1_d1),
    .c(decoder_8_bits_to_7_segment_1_c1));  // open: dp
  Decoder_8_bits_to_7_segment decoder_8_bits_to_7_segment_1 (
    .in_1(reg_8bit_2_b7), .d1(decoder_8_bits_to_7_segment_1_d1), .e1(decoder_8_bits_to_7_segment_1_e1),
    .f1(decoder_8_bits_to_7_segment_1_f1), .g1(decoder_8_bits_to_7_segment_1_g1),
    .a2(decoder_8_bits_to_7_segment_1_a2), .b2(decoder_8_bits_to_7_segment_1_b2),
    .c2(decoder_8_bits_to_7_segment_1_c2), .d2(decoder_8_bits_to_7_segment_1_d2),
    .e2(decoder_8_bits_to_7_segment_1_e2), .f2(decoder_8_bits_to_7_segment_1_f2),
    .g2(decoder_8_bits_to_7_segment_1_g2), .a3(decoder_8_bits_to_7_segment_1_a3),
    .b3(decoder_8_bits_to_7_segment_1_b3), .c3(decoder_8_bits_to_7_segment_1_c3),
    .d3(decoder_8_bits_to_7_segment_1_d3), .e3(decoder_8_bits_to_7_segment_1_e3),
    .f3(decoder_8_bits_to_7_segment_1_f3), .g3(decoder_8_bits_to_7_segment_1_g3),
    .a1(decoder_8_bits_to_7_segment_1_a1), .b1(decoder_8_bits_to_7_segment_1_b1),
    .c1(decoder_8_bits_to_7_segment_1_c1));

  // Notes on the sheet:
  //   D
  //   A
  //   Instruction
  //   Register
  //   C
  //   B
  //   Memory
  //   Register
  //   contents of rom_1 (hex, n*v repeats v):
  //   2 1 5 1 1f d 9 0 10 10 0 1f 14 5 1
endmodule
